// Logisim project 18-DDCA_Ch5-小班讨论题-寄存器文件(1).circ as structural Verilog: 1 circuit, main circuit ☆MIPS 寄存器文件
module \MIPS_寄存器文件  (
  input  [4:0] A_address,
  input  [31:0] W_data,
  input  [4:0] B_address,
  input  [4:0] W_address,
  input  W_Enable,
  input  CLK,
  output [31:0] A_data,
  output [31:0] B_data
);

  // RegisterFile registerfile_1: pin names not known; wires that end beside it: W_data, CLK, W_Enable, W_address, A_address, B_address, A_data, B_data

  // Other names for the same wires on the sheet: A_addr[4:0] = A_address; B_addr[4:0] = B_address;
  //   W_addr[4:0] = W_address

  // Notes on the sheet:
  //   输入引脚
  //   输出引脚
endmodule
