// Logisim project test1.circ as structural Verilog: 2 circuits, main circuit main
module main (
  input  in_1,
  input  in_2,
  input  in_3,
  input  in_4,
  input  in_5,
  output out_6,
  output out_7,
  output out_8,
  output out_9,
  output out_10
);

  or or_1 (out_6, in_1, in_2, in_3, in_4, in_5);
  or or_2 (out_7, in_2, in_3, in_4, in_5);
  or or_3 (out_8, in_3, in_4, in_5);
  or or_4 (out_9, in_4, in_5);

  assign out_10 = in_5;
endmodule

module test1 (
);

  wire button_1_out, button_2_out, button_3_out, button_4_out, main_1_out_6, main_1_out_7, main_1_out_8,
       main_1_out_9, main_1_out_10;

  Button button_1 (.out(button_1_out));
  Button button_2 (.out(button_2_out));
  Button button_3 (.out(button_3_out));
  Button button_4 (.out(button_4_out));
  Button button_5 (.out(button_4_out));
  main main_1 (
    .in_1(button_1_out), .in_2(button_2_out), .in_3(button_3_out), .in_4(button_4_out), .in_5(button_4_out),
    .out_6(main_1_out_6), .out_7(main_1_out_7), .out_8(main_1_out_8), .out_9(main_1_out_9),
    .out_10(main_1_out_10));
  LED #(.active("true")) led_1 (.in(main_1_out_6));
  LED #(.active("true")) led_2 (.in(main_1_out_7));
  LED #(.active("true")) led_3 (.in(main_1_out_8));
  LED #(.active("true")) led_4 (.in(main_1_out_9));
  LED #(.active("true")) led_5 (.in(main_1_out_10));
endmodule
