// Logisim project 七段数码管.circ as structural Verilog: 3 circuits, main circuit main
module main (
);

  wire A, a_t, and_1_out, and_2_out, B, b_t, C, c_t, comparator_1_eq, comparator_1_gt, D, d_t, E, e_t, F,
       f_t, G, g_t, or_1_out, \测试电路_1_out_1 , \测试电路_1_out_2 , \测试电路_1_out_3 , \测试电路_1_out_4 ;

  \测试电路  \u_测试电路_1  (.out_1(\测试电路_1_out_1 ), .out_2(\测试电路_1_out_2 ), .out_3(\测试电路_1_out_3 ), .out_4(\测试电路_1_out_4 ));
  and and_1 (and_1_out, \测试电路_1_out_3 , \测试电路_1_out_4 );
  and and_2 (and_2_out, \测试电路_1_out_2 , \测试电路_1_out_4 );
  Comparator #(.width(1), .mode("twosComplement")) comparator_1 (
    .a(and_1_out), .b(and_2_out), .gt(comparator_1_gt), .eq(comparator_1_eq));  // open: lt
  \译码电路  \u_译码电路_1  (
    .A0(\测试电路_1_out_1 ), .A1(\测试电路_1_out_2 ), .A2(\测试电路_1_out_3 ), .A3(\测试电路_1_out_4 ), .A(A), .B(B), .C(C),
    .D(D), .E(E), .F(F), .G(G));
  or or_1 (or_1_out, comparator_1_gt, comparator_1_eq);
  and and_3 (a_t, A, or_1_out);
  and and_4 (b_t, B, or_1_out);
  and and_5 (c_t, C, or_1_out);
  and and_6 (d_t, D, or_1_out);
  and and_7 (e_t, E, or_1_out);
  and and_8 (f_t, F, or_1_out);
  and and_9 (g_t, G, or_1_out);
  _7_Segment_Display #(.active("true")) u_7_segment_display_1 (
    .g(g_t), .f(f_t), .a(a_t), .b(b_t), .e(e_t), .d(d_t), .c(c_t));  // open: dp
endmodule

module \译码电路  (
  input  A0,
  input  A1,
  input  A2,
  input  A3,
  output A,
  output B,
  output C,
  output D,
  output E,
  output F,
  output G
);

  wire and_1_out, and_2_out, and_3_out, and_4_out, and_5_out, and_6_out, and_7_out, and_8_out, and_9_out,
       and_10_out, and_11_out, and_12_out, and_13_out, and_14_out, and_15_out, and_16_out, and_17_out,
       and_18_out, and_19_out, and_20_out, and_21_out, and_22_out, and_23_out, and_24_out, and_25_out,
       and_26_out, and_27_out, not_1_out, not_2_out, not_3_out, not_4_out, not_5_out, not_6_out, not_7_out,
       not_8_out, not_9_out, not_10_out, not_11_out, not_12_out, not_13_out, not_14_out, not_15_out,
       not_16_out, not_17_out, not_18_out, not_19_out, not_20_out, not_21_out, not_22_out, not_23_out,
       not_24_out, not_25_out, not_26_out, not_27_out, not_28_out, not_29_out, not_30_out, not_31_out,
       not_32_out, not_33_out, not_34_out, not_35_out, not_36_out, not_37_out, not_38_out, not_39_out,
       not_40_out, not_41_out, not_42_out, not_43_out, not_44_out, not_45_out, not_46_out, not_47_out,
       not_48_out, not_49_out, not_50_out, not_51_out, not_52_out, not_53_out, not_54_out, not_55_out,
       not_56_out;

  not not_1 (not_1_out, A0);
  and and_1 (and_1_out, not_1_out, not_2_out, not_3_out);
  not not_2 (not_2_out, A1);
  not not_3 (not_3_out, A2);
  not not_4 (not_4_out, A1);
  and and_2 (and_2_out, not_4_out, not_5_out, A3);
  not not_5 (not_5_out, A2);
  and and_3 (and_3_out, A1, not_6_out);
  not not_6 (not_6_out, A3);
  and and_4 (and_4_out, A0, A2, not_7_out);
  not not_7 (not_7_out, A3);
  not not_8 (not_8_out, A0);
  and and_5 (and_5_out, not_8_out, not_9_out, not_10_out);
  not not_9 (not_9_out, A1);
  not not_10 (not_10_out, A3);
  not not_11 (not_11_out, A0);
  not not_12 (not_12_out, A2);
  and and_6 (and_6_out, not_11_out, not_12_out, not_13_out);
  not not_13 (not_13_out, A3);
  not not_14 (not_14_out, A1);
  not not_15 (not_15_out, A2);
  and and_7 (and_7_out, not_14_out, not_15_out, A3);
  and and_8 (and_8_out, A0, A1, not_16_out);
  not not_16 (not_16_out, A3);
  not not_17 (not_17_out, A0);
  and and_9 (and_9_out, not_17_out, not_18_out, not_19_out);
  not not_18 (not_18_out, A1);
  not not_19 (not_19_out, A2);
  not not_20 (not_20_out, A1);
  and and_10 (and_10_out, not_20_out, not_21_out, A3);
  not not_21 (not_21_out, A2);
  and and_11 (and_11_out, A2, not_22_out);
  not not_22 (not_22_out, A3);
  and and_12 (and_12_out, A0, A1, not_23_out);
  not not_23 (not_23_out, A3);
  not not_24 (not_24_out, A0);
  not not_25 (not_25_out, A1);
  not not_26 (not_26_out, A2);
  not not_27 (not_27_out, A1);
  not not_28 (not_28_out, A2);
  not not_29 (not_29_out, A0);
  not not_30 (not_30_out, A3);
  not not_31 (not_31_out, A2);
  not not_32 (not_32_out, A3);
  not not_33 (not_33_out, A1);
  not not_34 (not_34_out, A3);
  not not_35 (not_35_out, A0);
  not not_36 (not_36_out, A1);
  and and_13 (and_13_out, not_35_out, not_36_out, not_37_out);
  not not_37 (not_37_out, A2);
  not not_38 (not_38_out, A1);
  and and_14 (and_14_out, not_38_out, not_39_out, not_40_out);
  not not_39 (not_39_out, A2);
  not not_40 (not_40_out, A3);
  not not_41 (not_41_out, A0);
  and and_15 (and_15_out, not_41_out, A1, not_42_out);
  not not_42 (not_42_out, A3);
  not not_43 (not_43_out, A1);
  and and_16 (and_16_out, not_43_out, not_44_out);
  not not_44 (not_44_out, A2);
  not not_45 (not_45_out, A1);
  and and_17 (and_17_out, not_45_out, not_46_out);
  not not_46 (not_46_out, A3);
  not not_47 (not_47_out, A0);
  and and_18 (and_18_out, not_47_out, A2, not_48_out);
  not not_48 (not_48_out, A3);
  not not_49 (not_49_out, A1);
  and and_19 (and_19_out, not_49_out, not_50_out, A3);
  not not_50 (not_50_out, A2);
  not not_51 (not_51_out, A1);
  and and_20 (and_20_out, not_51_out, A2, not_52_out);
  not not_52 (not_52_out, A3);
  not not_53 (not_53_out, A0);
  and and_21 (and_21_out, not_53_out, A1, not_54_out);
  not not_54 (not_54_out, A3);
  not not_55 (not_55_out, A2);
  and and_22 (and_22_out, A1, not_55_out, not_56_out);
  not not_56 (not_56_out, A3);
  or or_1 (A, and_1_out, and_2_out, and_3_out, and_4_out);
  or or_2 (B, and_5_out, and_6_out, and_7_out, and_8_out);
  or or_3 (C, and_9_out, and_10_out, and_11_out, and_12_out);
  and and_23 (and_23_out, not_24_out, not_25_out, not_26_out);
  and and_24 (and_24_out, not_27_out, not_28_out, A3);
  and and_25 (and_25_out, not_29_out, A1, not_30_out);
  and and_26 (and_26_out, A1, not_31_out, not_32_out);
  and and_27 (and_27_out, A0, not_33_out, A2, not_34_out);
  or or_4 (E, and_13_out, and_14_out, and_15_out);
  or or_5 (F, and_16_out, and_17_out, and_18_out);
  or or_6 (G, and_19_out, and_20_out, and_21_out, and_22_out);
  or or_7 (D, and_23_out, and_24_out, and_25_out, and_26_out, and_27_out);
endmodule

module \测试电路  (
  output out_1,
  output out_2,
  output out_3,
  output out_4
);

  wire clock_1_out, not_1_out, subtractor_1_bout;
  wire [3:0] counter_1_q, subtractor_1_out;

  not not_1 (not_1_out, subtractor_1_bout);
  Counter #(.width(4), .max('hf), .ongoal("wrap"), .trigger("rising"), .behavior("new")) counter_1 (
    .count(not_1_out), .Q(counter_1_q), .clk(clock_1_out), .clr(subtractor_1_bout));  // open: load, D, carry, preset, down
  Clock #(.highDuration(1), .lowDuration(1)) clock_1 (.out(clock_1_out));
  Subtractor #(.width(4)) subtractor_1 (
    .a(4'b0100), .b(counter_1_q), .out(subtractor_1_out), .bout(subtractor_1_bout));  // open: bin
  Adder #(.width(4)) adder_1 (
    .a(4'b0001), .b(subtractor_1_out), .out({out_4, out_3, out_2, out_1}));  // open: cin, cout
endmodule
