// Logisim project 乘法器问题.circ as structural Verilog: 3 circuits, main circuit main
module main (
  input  [7:0] X,
  input  [7:0] Y
);

  wire button_1_out, comparator_1_eq, DONE, load_A, load_B, load_P, OP, shift_A, shift_B;
  wire [2:0] register_4_q, \三个输入确定五种状态_1_s02 ;
  wire [7:0] multiplexer_2_out, register_3_q, shifter_2_out;
  wire [15:0] adder_1_out, bit_extender_1_out, multiplexer_1_out, register_1_q, register_2_q, shifter_1_out;

  assign bit_extender_1_out = {{8{1'b0}}, X};  // Bit_Extender bit_extender_1
  Multiplexer #(.select(1), .width(16), .disabled("Z"), .enable("false")) multiplexer_1 (
    .in0(bit_extender_1_out), .in1(shifter_1_out), .out(multiplexer_1_out), .sel(shift_A));
  Register #(.width(16), .trigger("rising"), .Select("low")) register_1 (
    .D(multiplexer_1_out), .en(load_A), .Q(register_1_q));  // open: clk, clr
  Shifter #(.width(16), .shift("ll")) shifter_1 (.in(register_1_q), .\dist (4'b0001), .out(shifter_1_out));
  Register #(.width(16), .trigger("rising"), .Select("low")) register_2 (
    .D(adder_1_out), .en(load_P), .Q(register_2_q));  // open: clk, clr
  Adder #(.width(16)) adder_1 (.a(register_1_q), .b(register_2_q), .out(adder_1_out));  // open: cin, cout
  Button button_1 (.out(button_1_out));
  Multiplexer #(.select(1), .width(8), .disabled("Z"), .enable("false")) multiplexer_2 (
    .in0(Y), .in1(shifter_2_out), .out(multiplexer_2_out), .sel(shift_B));
  Register #(.width(8), .trigger("rising"), .Select("low")) register_3 (
    .D(multiplexer_2_out), .en(load_B), .Q(register_3_q));  // open: clk, clr
  Shifter #(.width(8), .shift("lr")) shifter_2 (.in(register_3_q), .\dist (3'b001), .out(shifter_2_out));
  Comparator #(.width(8), .mode("twosComplement")) comparator_1 (
    .a(register_3_q), .b({8{1'b0}}), .eq(comparator_1_eq));  // open: gt, lt
  \三个输入确定五种状态  \u_三个输入确定五种状态_1  (
    .S0(register_4_q[0]), .S1(register_4_q[1]), .S2(button_1_out), .start(comparator_1_eq),
    .zero(register_3_q[0]), .S02(\三个输入确定五种状态_1_s02 [0]), .S12(\三个输入确定五种状态_1_s02 [1]),
    .S22(\三个输入确定五种状态_1_s02 [2]));  // open: B0
  Register #(.width(3), .trigger("rising"), .Select("low")) register_4 (
    .D(\三个输入确定五种状态_1_s02 ), .Q(register_4_q));  // open: en, clk, clr
  \五种状态确定七个动作  \u_五种状态确定七个动作_1  (
    .S1(register_4_q[0]), .S2(register_4_q[2]), .DONE(register_4_q[1]), .LA(load_A), .LB(load_B),
    .LP(load_P), .SB(shift_B), .SA(shift_A), .OP(OP), .DONE_2(DONE));
endmodule

module \三个输入确定五种状态  (
  input  S0,
  input  S1,
  input  S2,
  input  start,
  input  zero,
  input  B0,
  output S02,
  output S12,
  output S22
);

  wire and_1_out, and_3_out, and_4_out, and_5_out, not_1_out, not_2_out, not_3_out, not_4_out, not_5_out,
       not_6_out, not_7_out, not_8_out, not_9_out;

  not not_1 (not_1_out, S1);
  not not_2 (not_2_out, S1);
  not not_3 (not_3_out, zero);
  not not_4 (not_4_out, S0);
  not not_5 (not_5_out, S2);
  not not_6 (not_6_out, S2);
  not not_7 (not_7_out, zero);
  not not_8 (not_8_out, B0);
  not not_9 (not_9_out, zero);
  and and_1 (and_1_out, not_1_out, S2, zero);
  and and_2 (S12, not_2_out, S2, not_3_out);
  and and_3 (and_3_out, not_4_out, not_5_out, start);
  and and_4 (and_4_out, not_6_out, start, not_7_out, not_8_out);
  and and_5 (and_5_out, S2, not_9_out, B0);
  or or_1 (S02, and_1_out, S0);
  or or_2 (S22, and_3_out, and_4_out, and_5_out, S1);
endmodule

module \五种状态确定七个动作  (
  input  S1,
  input  S2,
  input  DONE,
  output LA,
  output LB,
  output LP,
  output SB,
  output SA,
  output OP,
  output DONE_2
);

  wire not_1_out, not_2_out, not_3_out, not_4_out, not_5_out, not_6_out;

  not not_1 (not_1_out, S1);
  not not_2 (not_2_out, S2);
  not not_3 (not_3_out, S1);
  not not_4 (not_4_out, S2);
  not not_5 (not_5_out, S1);
  not not_6 (not_6_out, S2);
  and and_1 (OP, S1, S2);
  and and_2 (LA, not_1_out, not_2_out);
  and and_3 (LB, not_3_out, not_4_out);
  and and_4 (LP, not_5_out, not_6_out);

  assign DONE_2 = DONE;
  assign SA = S1;
  assign SB = S1;
endmodule
