// Logisim project 作业 - ALU.circ as structural Verilog: 5 circuits, main circuit ☆算术逻辑运算单元ALU
// ALU
module \算术逻辑运算单元ALU  (
  input  [31:0] X,
  input  [31:0] Y,
  input  [2:0] AluOP,
  output \结果是否为0 ,
  output [31:0] Result
);

  wire comparator_1_lt;
  wire [24:0] \运算指示 ;
  wire [31:0] adder_1_out, AND_out, bit_extender_1_out, multiplexer_1_out, multiplexer_2_out, not_1_out,
       OR_out, subtractor_1_out;

  // Probe on X
  // Probe on X
  // Probe on Y
  // Probe on Y
  assign not_1_out = ~Y;  // NOT_Gate not_1, 32 bits wide
  // Probe on AluOP
  Multiplexer #(.select(1), .width(32), .disabled("Z"), .enable("false")) multiplexer_1 (
    .in0(Y), .in1(not_1_out), .out(multiplexer_1_out), .sel(AluOP[2]));
  // Probe on Result
  // Probe on Result
  DotMatrix #(.inputtype("column"), .matrixcols(5), .matrixrows(5), .persist(0), .dotshape("square")) dotmatrix_1 (
    .col0(\运算指示 [24:20]), .col1(\运算指示 [19:15]), .col2(\运算指示 [14:10]), .col3(\运算指示 [9:5]), .col4(\运算指示 [4:0]));
  Adder #(.width(32)) adder_1 (.a(X), .b(Y), .out(adder_1_out));  // open: cin, cout
  Subtractor #(.width(32)) subtractor_1 (.a(X), .b(Y), .out(subtractor_1_out));  // open: bin, bout
  assign AND_out = X & multiplexer_1_out;  // AND_Gate AND, 32 bits wide
  assign OR_out = X | multiplexer_1_out;  // OR_Gate OR, 32 bits wide
  Comparator #(.width(32), .mode("twosComplement")) comparator_1 (.a(X), .b(Y), .lt(comparator_1_lt));  // open: gt, eq
  Multiplexer #(.select(1), .width(32), .disabled("Z"), .enable("false")) multiplexer_2 (
    .in0(adder_1_out), .in1(subtractor_1_out), .out(multiplexer_2_out), .sel(AluOP[0]));
  assign bit_extender_1_out = {{31{1'b0}}, comparator_1_lt};  // Bit_Extender bit_extender_1
  Multiplexer #(.select(2), .width(32), .disabled("Z"), .enable("false")) multiplexer_3 (
    .in0(AND_out), .in1(OR_out), .in2(multiplexer_2_out), .in3(bit_extender_1_out), .out(Result),
    .sel(AluOP[1:0]));
  Multiplexer #(.select(3), .width(25), .disabled("Z"), .enable("false")) multiplexer_4 (
    .in0(25'h124081), .in1(25'h1020490), .in2(25'h427c84), .in3({25{1'b0}}), .in4(25'h124091),
    .in5(25'h1020490), .in6(25'h421084), .in7(25'h402811), .out(\运算指示 ), .sel(AluOP));
  Comparator #(.width(32), .mode("twosComplement")) comparator_2 (
    .a(Result), .b({32{1'b0}}), .eq(\结果是否为0 ));  // open: gt, lt

  // Other names for the same wires on the sheet: S[2:0] = AluOP; Zero = \结果是否为0 

  // Notes on the sheet:
  //   AluOP: pull=down
  //   X: pull=down
  //   Y: pull=down
  //   不要改变此引脚区域内容，也不要改变ALU封装形式
  //   请在下方利用上方输入输出引脚的隧道信号构建ALU电路，ctrl+d复制选择部件
  //   输入引脚
  //   探测区域
  //   输出引脚
  //   功能说明：
  //   000：X AND Y      100：X AND Y'
  //   001：X OR Y        101：X OR Y'  
  //   010：X + Y           110：X - Y  
  //   011：未使用         111：SLT  
endmodule

module \ALU自动测试  (
  output [7:0] TEST_num
);

  wire ADD, AND, and_1_out, AND_prime, CLK, comparator_2_eq, HALT, Halt_t, multiplexer_1_out, nHalt, NotEQ,
       OR, OR_prime, priority_encoder_1_gs, Rok, SLT, SUB, X___Y, X___Y_t, X_AND_Y, X_AND_Y_prime, X_OR_Y,
       X_OR_Y_prime, X_Y, xnor_1_out, Zero, Zero_Standard, \悬空检测 ;
  wire [2:0] ALUOP;
  wire [3:0] \个位 , \十位 , \百位 ;
  wire [7:0] adder_1_out, \单项评分_1_总条数 , \单项评分_1_扣分 , \单项评分_1_正确条数 , \单项评分_2_总条数 , \单项评分_2_扣分 , \单项评分_2_正确条数 ,
       \单项评分_3_总条数 , \单项评分_3_扣分 , \单项评分_3_正确条数 , \单项评分_4_总条数 , \单项评分_4_扣分 , \单项评分_4_正确条数 , \单项评分_5_总条数 ,
       \单项评分_5_扣分 , \单项评分_5_正确条数 , \单项评分_6_总条数 , \单项评分_6_扣分 , \单项评分_6_正确条数 , \单项评分_7_总条数 , \单项评分_7_扣分 ,
       \单项评分_7_正确条数 , \单项评分_8_扣分 , \总项评分_1_总分 ;
  wire [9:0] counter_1_q;
  wire [31:0] bit_extender_1_out, R, R_Standard, X, Y;

  Register #(.width(8), .trigger("rising"), .Select("low")) register_1 (
    .D(adder_1_out), .en(nHalt), .Q(TEST_num), .clk(CLK));  // open: clr
  Clock #(.highDuration(1), .lowDuration(1)) clock_1 (.out(CLK));
  \单项评分  \u_单项评分_1  (
    .ALUOP(AND), .\扣分 (\单项评分_1_扣分 ), .\正确条数 (\单项评分_1_正确条数 ), .Rok(Rok), .nHalt(nHalt), .Right(X_AND_Y),
    .CLK(CLK), .\总条数 (\单项评分_1_总条数 ), .NotEQ(NotEQ));
  // Probe on \单项评分_1_总条数 
  // Probe on \单项评分_1_正确条数 
  // Probe on \单项评分_1_扣分 
  Adder #(.width(8)) adder_1 (.a(8'h1), .b(TEST_num), .out(adder_1_out));  // open: cin, cout
  not not_1 (nHalt, Halt_t);
  Comparator #(.width(3), .mode("twosComplement")) comparator_1 (.a(ALUOP), .b(3'b011), .eq(Halt_t));  // open: gt, lt
  Counter #(.width(10), .max('h3ff), .ongoal("wrap"), .trigger("rising"), .behavior("old")) counter_1 (
    .count(NotEQ), .Q(counter_1_q), .clk(CLK), .clr(Halt_t));  // open: load, D, carry, preset
  and and_1 (and_1_out, ~Halt_t, NotEQ);  // AND_Gate
  \单项评分  \u_单项评分_2  (
    .ALUOP(OR), .\扣分 (\单项评分_2_扣分 ), .\正确条数 (\单项评分_2_正确条数 ), .Rok(Rok), .nHalt(nHalt), .Right(X_OR_Y),
    .CLK(CLK), .\总条数 (\单项评分_2_总条数 ), .NotEQ(NotEQ));
  // Probe on \单项评分_2_总条数 
  // Probe on \单项评分_2_正确条数 
  // Probe on \单项评分_2_扣分 
  \总项评分  \u_总项评分_1  (
    .in_1(\单项评分_1_扣分 ), .in_2(\单项评分_2_扣分 ), .in_3(\单项评分_3_扣分 ), .in_4(\单项评分_4_扣分 ), .in_5(\单项评分_5_扣分 ),
    .in_6(\单项评分_6_扣分 ), .in_8(\单项评分_7_扣分 ), .in_9(\单项评分_8_扣分 ), .\总分 (\总项评分_1_总分 ), .\百位 (\百位 ), .\十位 (\十位 ),
    .\个位 (\个位 ), .\Zero悬空扣分 (\悬空检测 ));
  trace trace_1 (.in_1(TEST_num), .X(X), .Y(Y), .AluOP(ALUOP), .R(R_Standard), .Zero(Zero_Standard));
  \单项评分  \u_单项评分_3  (
    .ALUOP(ADD), .\扣分 (\单项评分_3_扣分 ), .\正确条数 (\单项评分_3_正确条数 ), .Rok(Rok), .nHalt(nHalt), .Right(X___Y),
    .CLK(CLK), .\总条数 (\单项评分_3_总条数 ), .NotEQ(NotEQ));
  // Probe on \单项评分_3_总条数 
  // Probe on \单项评分_3_正确条数 
  // Probe on \单项评分_3_扣分 
  RAM #(.addrWidth(10), .dataWidth(32), .bus("separate"), .Select("low")) ram_1 (
    .addr(counter_1_q), .din(X), .str(and_1_out), .clk(CLK));  // open: data, sel, ld, clr
  \单项评分  \u_单项评分_4  (
    .ALUOP(AND_prime), .\扣分 (\单项评分_4_扣分 ), .\正确条数 (\单项评分_4_正确条数 ), .Rok(Rok), .nHalt(nHalt),
    .Right(X_AND_Y_prime), .CLK(CLK), .\总条数 (\单项评分_4_总条数 ), .NotEQ(NotEQ));
  // Probe on \单项评分_4_总条数 
  // Probe on \单项评分_4_正确条数 
  // Probe on \单项评分_4_扣分 
  \单项评分  \u_单项评分_5  (
    .ALUOP(OR_prime), .\扣分 (\单项评分_5_扣分 ), .\正确条数 (\单项评分_5_正确条数 ), .Rok(Rok), .nHalt(nHalt),
    .Right(X_OR_Y_prime), .CLK(CLK), .\总条数 (\单项评分_5_总条数 ), .NotEQ(NotEQ));
  // Probe on \单项评分_5_总条数 
  // Probe on \单项评分_5_正确条数 
  // Probe on \单项评分_5_扣分 
  // Probe on \总项评分_1_总分 
  \算术逻辑运算单元ALU  \u_算术逻辑运算单元alu_1  (.AluOP(ALUOP), .X(X), .Result(R), .Y(Y), .\结果是否为0 (Zero));
  RAM #(.addrWidth(10), .dataWidth(32), .bus("separate"), .Select("low")) ram_2 (
    .addr(counter_1_q), .din(Y), .str(and_1_out), .clk(CLK));  // open: data, sel, ld, clr
  assign bit_extender_1_out = {{29{1'b0}}, ALUOP};  // Bit_Extender bit_extender_1
  \单项评分  \u_单项评分_6  (
    .ALUOP(SUB), .\扣分 (\单项评分_6_扣分 ), .\正确条数 (\单项评分_6_正确条数 ), .Rok(Rok), .nHalt(nHalt), .Right(X___Y_t),
    .CLK(CLK), .\总条数 (\单项评分_6_总条数 ), .NotEQ(NotEQ));
  // Probe on \单项评分_7_总条数 
  // Probe on \单项评分_6_总条数 
  // Probe on \单项评分_6_正确条数 
  // Probe on \单项评分_6_扣分 
  \单项评分  \u_单项评分_7  (
    .ALUOP(SLT), .\扣分 (\单项评分_7_扣分 ), .\正确条数 (\单项评分_7_正确条数 ), .Rok(Rok), .nHalt(nHalt), .Right(X_Y),
    .CLK(CLK), .\总条数 (\单项评分_7_总条数 ), .NotEQ(NotEQ));
  // Probe on \单项评分_7_正确条数 
  // Probe on \单项评分_7_扣分 
  // Probe on ALUOP
  \单项评分  \u_单项评分_8  (
    .ALUOP(1'b0), .\扣分 (\单项评分_8_扣分 ), .Rok(Rok), .nHalt(nHalt), .CLK(CLK), .NotEQ(NotEQ));  // open: 正确条数, Right, 总条数
  RAM #(.addrWidth(10), .dataWidth(32), .bus("separate"), .Select("low")) ram_3 (
    .addr(counter_1_q), .din(bit_extender_1_out), .str(and_1_out), .clk(CLK));  // open: data, sel, ld, clr
  Decoder #(.select(3), .tristate("false"), .disabled("Z"), .enable("false")) decoder_1 (
    .out0(AND), .out1(OR), .out2(ADD), .out3(HALT), .out4(AND_prime), .out5(OR_prime), .out6(SUB),
    .out7(SLT), .sel(ALUOP));
  Multiplexer #(.select(1), .width(1), .disabled("Z"), .enable("false")) multiplexer_1 (
    .in0(1'b1), .in1(1'b1), .out(multiplexer_1_out), .sel(Zero));
  xnor xnor_1 (xnor_1_out, Zero_Standard, Zero);
  Comparator #(.width(32), .mode("twosComplement")) comparator_2 (
    .a(R_Standard), .b(R), .eq(comparator_2_eq));  // open: gt, lt
  LED #(.active("false")) led_1 (.in(X_AND_Y));
  LED #(.active("false")) led_2 (.in(X_OR_Y));
  LED #(.active("false")) led_3 (.in(X___Y));
  LED #(.active("false")) led_4 (.in(X_AND_Y_prime));
  LED #(.active("false")) led_5 (.in(X_OR_Y_prime));
  LED #(.active("false")) led_6 (.in(X___Y_t));
  LED #(.active("false")) led_7 (.in(X_Y));
  LED #(.active("true")) led_8 (.in(NotEQ));
  Priority_Encoder #(.select(1), .disabled("Z")) priority_encoder_1 (
    .in0(multiplexer_1_out), .in1(multiplexer_1_out), .gs(priority_encoder_1_gs));  // open: out, en_out, en_in
  not not_2 (\悬空检测 , priority_encoder_1_gs);
  nand nand_1 (NotEQ, xnor_1_out, Rok);
  Priority_Encoder #(.select(1), .disabled("Z")) priority_encoder_2 (
    .in0(comparator_2_eq), .in1(comparator_2_eq), .gs(Rok));  // open: out, en_out, en_in
  Hex_Digit_Display hex_digit_display_1 (.value(\百位 ));  // open: dp
  Hex_Digit_Display hex_digit_display_2 (.value(\十位 ));  // open: dp
  Hex_Digit_Display hex_digit_display_3 (.value(\个位 ));  // open: dp

  // Notes on the sheet:
  //   X 错误记录
  //   Y 错误记录
  //   ALUOP 错误记录
  //   运算故障指示
  //   红色异常
  //   成绩
endmodule

module trace (
  input  [7:0] in_1,
  output [31:0] X,
  output [31:0] Y,
  output [2:0] AluOP,
  output [31:0] R,
  output Zero
);

  ROM #(.addrWidth(8), .dataWidth(32), .Select("high")) rom_1 (.addr(in_1), .data(X));
  ROM #(.addrWidth(8), .dataWidth(32), .Select("high")) rom_2 (.addr(in_1), .data(Y));
  ROM #(.addrWidth(8), .dataWidth(3), .Select("high")) rom_3 (.addr(in_1), .data(AluOP));
  ROM #(.addrWidth(8), .dataWidth(32), .Select("high")) rom_4 (.addr(in_1), .data(R));
  ROM #(.addrWidth(8), .dataWidth(1), .Select("high")) rom_5 (.addr(in_1), .data(Zero));

  // Notes on the sheet:
  //   X trace
  //   contents of rom_1 (hex, n*v repeats v):
  //   1 1 1 0 11111111 0 0 0 10b67f2
  //   Y trace
  //   contents of rom_2 (hex, n*v repeats v):
  //   1 0 1 4*0 1 2f5a0df4
  //   ALU OP Trace
  //   contents of rom_3 (hex, n*v repeats v):
  //   0 1 2 0 4 5 6 7 2
  //   Result
  //   contents of rom_4 (hex, n*v repeats v):
  //   1 1 2 0 11111111 ffffffff 0 1 306575e6
  //   Zero Flag
  //   contents of rom_5 (hex, n*v repeats v):
  //   0 0 0 1 0 0 1 0 0 247*1
endmodule

module \单项评分  (
  input  ALUOP,
  input  NotEQ,
  input  Rok,
  input  nHalt,
  input  CLK,
  output [7:0] \扣分 ,
  output [7:0] \正确条数 ,
  output Right,
  output [7:0] \总条数 
);

  wire and_1_out, and_2_out, and_3_out, and_4_out, comparator_1_eq, not_1_out, not_2_out, not_3_out,
       undriven, undriven_2, undriven_3, undriven_4;
  wire [7:0] counter_1_q, counter_2_q, multiplexer_1_out;

  not not_1 (not_1_out, NotEQ);
  and and_1 (and_1_out, undriven, undriven_2, undriven_3);
  and and_2 (and_2_out, undriven, undriven_3);
  and and_3 (and_3_out, ALUOP, not_1_out, Rok, nHalt);
  and and_4 (and_4_out, ALUOP, nHalt);
  Counter #(.width(8), .max('hff), .ongoal("wrap"), .trigger("rising"), .behavior("new")) counter_1 (
    .Q(counter_1_q), .clk(undriven_4), .down(and_1_out));  // open: load, D, count, carry, clr, preset
  Counter #(.width(8), .max('hff), .ongoal("wrap"), .trigger("rising"), .behavior("new")) counter_2 (
    .Q(counter_2_q), .down(and_2_out));  // open: load, D, count, carry, clk, clr, preset
  Counter #(.width(8), .max('hff), .ongoal("wrap"), .trigger("rising"), .behavior("old")) counter_3 (
    .count(and_3_out), .Q(\正确条数 ), .clk(CLK));  // open: load, D, carry, clr, preset
  Counter #(.width(8), .max('hff), .ongoal("wrap"), .trigger("rising"), .behavior("old")) counter_4 (
    .count(and_4_out), .Q(\总条数 ), .clk(CLK));  // open: load, D, carry, clr, preset
  Comparator #(.width(8), .mode("twosComplement")) comparator_1 (
    .a(counter_1_q), .b(counter_2_q), .eq(comparator_1_eq));  // open: gt, lt
  Comparator #(.width(8), .mode("twosComplement")) comparator_2 (.a(\正确条数 ), .b(\总条数 ), .eq(Right));  // open: gt, lt
  Multiplexer #(.select(1), .width(8), .disabled("Z"), .enable("false")) multiplexer_1 (
    .in0({8{1'b0}}), .in1(8'h5), .out(multiplexer_1_out), .sel(not_2_out));
  not not_2 (not_2_out, comparator_1_eq);
  not not_3 (not_3_out, Right);
  Multiplexer #(.select(1), .width(8), .disabled("Z"), .enable("false")) multiplexer_2 (
    .in0({8{1'b0}}), .in1(8'h5), .out(\扣分 ), .sel(not_3_out));

  // Notes on the sheet:
  //   ALUOP
  //   Rok
  //   ~Halt
  //   CLK
  //   Duplicated
  //   总条数
  //   正确条数
  //   扣分
  //   Right？
endmodule

module \总项评分  (
  input  [7:0] in_1,
  input  [7:0] in_2,
  input  [7:0] in_3,
  input  [7:0] in_4,
  input  [7:0] in_5,
  input  [7:0] in_6,
  input  \Zero悬空扣分 ,
  input  [7:0] in_8,
  input  [7:0] in_9,
  output [7:0] \总分 ,
  output [3:0] \百位 ,
  output [3:0] \十位 ,
  output [3:0] \个位 
);

  wire [7:0] adder_1_out, adder_2_out, adder_3_out, adder_4_out, adder_5_out, adder_6_out, adder_7_out,
       divider_1_out, subtractor_1_out, subtractor_2_out;
  wire [7:4] divider_1_rem, divider_2_out, divider_2_rem;

  Adder #(.width(8)) adder_1 (.a(in_1), .b(in_2), .out(adder_1_out));  // open: cin, cout
  Adder #(.width(8)) adder_2 (.a(in_3), .b(in_4), .out(adder_2_out));  // open: cin, cout
  Adder #(.width(8)) adder_3 (.a(in_5), .b(in_6), .out(adder_3_out));  // open: cin, cout
  Adder #(.width(8)) adder_4 (.a(in_8), .b(in_9), .out(adder_4_out));  // open: cin, cout
  Adder #(.width(8)) adder_5 (.a(adder_1_out), .b(adder_2_out), .out(adder_5_out));  // open: cin, cout
  Adder #(.width(8)) adder_6 (.a(adder_3_out), .b(adder_4_out), .out(adder_6_out));  // open: cin, cout
  Adder #(.width(8)) adder_7 (.a(adder_5_out), .b(adder_6_out), .out(adder_7_out));  // open: cin, cout
  Subtractor #(.width(8)) subtractor_1 (.a(8'h64), .b(adder_7_out), .out(subtractor_1_out));  // open: bin, bout
  Subtractor #(.width(8)) subtractor_2 (.a(subtractor_1_out), .b(8'h5), .out(subtractor_2_out));  // open: bin, bout
  Multiplexer #(.select(1), .width(8), .disabled("Z"), .enable("false")) multiplexer_1 (
    .in0(subtractor_1_out), .in1(subtractor_2_out), .out(\总分 ), .sel(\Zero悬空扣分 ));
  Divider #(.width(8)) divider_1 (.a(\总分 ), .b(8'ha), .out(divider_1_out), .rem({divider_1_rem, \个位 }));  // open: upper
  Divider #(.width(8)) divider_2 (
    .a(divider_1_out), .b(8'ha), .out({divider_2_out, \百位 }), .rem({divider_2_rem, \十位 }));  // open: upper
endmodule
