// Logisim project 作业 - 乘法器.circ as structural Verilog: 3 circuits, main circuit main
module main (
  input  in_1,
  input  [7:0] X,
  input  [7:0] Y,
  output [15:0] out_4,
  output out_5
);

  wire clk, comparator_1_eq, load_A, load_B, load_P, OP, shift_A, shift_B;
  wire [2:0] register_3_q, \三个输入确定五种状态_1_s02 ;
  wire [7:0] multiplexer_2_out, register_2_q, shifter_2_out;
  wire [15:0] adder_1_out, bit_extender_1_out, multiplexer_1_out, register_1_q, shifter_1_out;

  Clock #(.highDuration(1), .lowDuration(1)) clock_1 (.out(clk));
  assign bit_extender_1_out = {{8{1'b0}}, X};  // Bit_Extender bit_extender_1
  Multiplexer #(.select(1), .width(16), .disabled("Z"), .enable("false")) multiplexer_1 (
    .in0(bit_extender_1_out), .in1(shifter_1_out), .out(multiplexer_1_out), .sel(shift_A));
  Register #(.width(16), .trigger("rising"), .Select("low")) register_1 (
    .D(multiplexer_1_out), .en(load_A), .Q(register_1_q), .clk(clk));  // open: clr
  Shifter #(.width(16), .shift("ll")) shifter_1 (.in(register_1_q), .\dist (4'b0001), .out(shifter_1_out));
  Adder #(.width(16)) adder_1 (.a(register_1_q), .b(out_4), .out(adder_1_out));  // open: cin, cout
  Register #(.width(16), .trigger("rising"), .Select("low")) p (
    .D(adder_1_out), .en(load_P), .Q(out_4), .clk(clk));  // open: clr
  Multiplexer #(.select(1), .width(8), .disabled("Z"), .enable("false")) multiplexer_2 (
    .in0(Y), .in1(shifter_2_out), .out(multiplexer_2_out), .sel(shift_B));
  Register #(.width(8), .trigger("rising"), .Select("low")) register_2 (
    .D(multiplexer_2_out), .en(load_B), .Q(register_2_q), .clk(clk));  // open: clr
  Shifter #(.width(8), .shift("lr")) shifter_2 (.in(register_2_q), .\dist (3'b001), .out(shifter_2_out));
  Comparator #(.width(8), .mode("twosComplement")) comparator_1 (
    .a(register_2_q), .b({8{1'b0}}), .eq(comparator_1_eq));  // open: gt, lt
  \三个输入确定五种状态  \u_三个输入确定五种状态_1  (
    .S0(register_3_q[0]), .S1(register_3_q[1]), .S2(register_3_q[2]), .start(in_1), .zero(comparator_1_eq),
    .B0(register_2_q[0]), .S02(\三个输入确定五种状态_1_s02 [0]), .S12(\三个输入确定五种状态_1_s02 [1]),
    .S22(\三个输入确定五种状态_1_s02 [2]));
  Register #(.width(3), .trigger("rising"), .Select("low")) register_3 (
    .D(\三个输入确定五种状态_1_s02 ), .Q(register_3_q), .clk(clk));  // open: en, clr
  \五种状态确定七个动作  \u_五种状态确定七个动作_1  (
    .S0(register_3_q[0]), .S1(register_3_q[1]), .S2(register_3_q[2]), .LA(load_A), .LB(load_B), .LP(load_P),
    .SB(shift_B), .SA(shift_A), .OP(OP), .DONE(out_5));
endmodule

module \三个输入确定五种状态  (
  input  S0,
  input  S1,
  input  S2,
  input  start,
  input  zero,
  input  B0,
  output S02,
  output S12,
  output S22
);

  wire and_1_out, and_3_out, and_4_out, and_5_out, not_1_out, not_2_out, not_3_out, not_4_out, not_5_out,
       not_6_out, not_7_out, not_8_out, not_9_out;

  not not_1 (not_1_out, S1);
  not not_2 (not_2_out, S0);
  not not_3 (not_3_out, S1);
  not not_4 (not_4_out, zero);
  not not_5 (not_5_out, S0);
  not not_6 (not_6_out, S2);
  not not_7 (not_7_out, S0);
  not not_8 (not_8_out, zero);
  not not_9 (not_9_out, S0);
  and and_1 (and_1_out, not_1_out, S2, zero);
  and and_2 (S12, not_2_out, not_3_out, S2, not_4_out);
  and and_3 (and_3_out, not_5_out, not_6_out, start);
  and and_4 (and_4_out, not_7_out, S2, not_8_out, B0);
  and and_5 (and_5_out, not_9_out, S1);
  or or_1 (S02, and_1_out, S0);
  or or_2 (S22, and_3_out, and_4_out, and_5_out);
endmodule

module \五种状态确定七个动作  (
  input  S0,
  input  S1,
  input  S2,
  output LA,
  output LB,
  output LP,
  output SB,
  output SA,
  output OP,
  output DONE
);

  wire and_1_out, and_2_out, and_3_out, and_4_out, and_5_out, and_6_out, not_1_out, not_2_out, not_3_out,
       not_4_out, not_5_out, not_6_out, not_7_out, not_8_out, not_9_out, not_10_out, not_11_out, not_12_out,
       not_13_out;

  not not_1 (not_1_out, S0);
  not not_2 (not_2_out, S2);
  not not_3 (not_3_out, S0);
  not not_4 (not_4_out, S0);
  not not_5 (not_5_out, S2);
  not not_6 (not_6_out, S0);
  not not_7 (not_7_out, S0);
  not not_8 (not_8_out, S1);
  not not_9 (not_9_out, S2);
  not not_10 (not_10_out, S0);
  not not_11 (not_11_out, S0);
  not not_12 (not_12_out, S0);
  not not_13 (not_13_out, S0);
  and and_1 (and_1_out, not_1_out, not_2_out);
  and and_2 (and_2_out, not_3_out, S1);
  and and_3 (and_3_out, not_4_out, not_5_out);
  and and_4 (and_4_out, not_6_out, S1);
  and and_5 (and_5_out, not_7_out, not_8_out, not_9_out);
  and and_6 (and_6_out, not_10_out, S1, S2);
  and and_7 (SB, not_11_out, S1);
  and and_8 (SA, not_12_out, S1);
  and and_9 (OP, not_13_out, S1, S2);
  or or_1 (LA, and_1_out, and_2_out);
  or or_2 (LB, and_3_out, and_4_out);
  or or_3 (LP, and_5_out, and_6_out);

  assign DONE = S0;
endmodule
