// Logisim project 作业 - 存储器.circ as structural Verilog: 1 circuit, main circuit main
module main (
  input  W,
  input  R,
  input  in_3,
  input  [15:0] address,
  input  [7:0] data,
  output [7:0] data_out
);

  wire and_1_out, C, cs0_out, cs1_out, cs3_out, cs4_out, nand_1_out, not_2_out, not_3_out, not_4_out,
       not_5_out, not_6_out;

  // NOT_Gate not_1 has open pins: in=in_3, out=open
  Clock #(.highDuration(1), .lowDuration(1)) clock_1 (.out(C));
  and cs0 (cs0_out, ~address[11], ~address[12], ~address[13]);  // AND_Gate
  not not_2 (not_2_out, cs0_out);
  not not_3 (not_3_out, cs1_out);
  and cs1 (cs1_out, address[11], ~address[11], ~address[11]);  // AND_Gate
  and cs3 (cs3_out, address[11], address[11], address[11], ~address[14], ~address[15]);  // AND_Gate
  not not_4 (not_4_out, cs3_out);
  and cs4 (cs4_out, address[11], address[11], address[11], ~address[14], address[15]);  // AND_Gate
  not not_5 (not_5_out, cs4_out);
  nand nand_1 (nand_1_out, address[11], address[11], address[11], address[14], ~address[15]);  // NAND_Gate
  not not_6 (not_6_out, and_1_out);
  and and_1 (and_1_out, address[11], address[11], address[11], address[14], address[15]);
  RAM #(.addrWidth(16), .dataWidth(8), .bus("separate"), .Select("low")) \u_用户ram  (
    .addr(address), .din(data), .data(data_out), .str(W), .sel(not_2_out), .clk(C), .ld(R));  // open: clr
  RAM #(.addrWidth(16), .dataWidth(8), .bus("separate"), .Select("low")) \u_程序工程ram  (
    .addr(address), .din(data), .data(data_out), .str(W), .sel(not_4_out), .clk(C), .ld(R));  // open: clr
  ROM #(.addrWidth(16), .dataWidth(8), .Select("low")) \u_系统区rom  (.addr(address), .data(data_out), .sel(nand_1_out));
  RAM #(.addrWidth(16), .dataWidth(8), .bus("separate"), .Select("low")) \u_用户ram_2  (
    .addr(address), .din(data), .data(data_out), .str(W), .sel(not_3_out), .clk(C), .ld(R));  // open: clr
  RAM #(.addrWidth(16), .dataWidth(8), .bus("separate"), .Select("low")) \u_程序工程ram_2  (
    .addr(address), .din(data), .data(data_out), .str(W), .sel(not_5_out), .clk(C), .ld(R));  // open: clr
  ROM #(.addrWidth(16), .dataWidth(8), .Select("low")) \u_系统区rom_2  (.addr(address), .data(data_out), .sel(not_6_out));

  // Other names for the same wires on the sheet: data_in[7:0] = data
endmodule
