// Logisim project 单周期.circ as structural Verilog: 17 circuits, main circuit ☆单周期处理器数据路径
module \存储器扩展  (
  input  [15:0] Addr,
  input  [7:0] Data,
  input  R_W_prime,
  input  MREQ_prime,
  output [7:0] Data_2
);

  wire CLK, CS1, CS2, CS3, CS4, CS5, ld, not_1_out, not_2_out, not_3_out, not_4_out, not_5_out, not_6_out,
       not_7_out, not_8_out, not_9_out, not_10_out, not_11_out, not_12_out, not_13_out, not_14_out,
       not_15_out, or_1_out, or_3_out, or_5_out, or_6_out, or_7_out, or_8_out, or_10_out, or_11_out,
       or_12_out, or_13_out, str;

  Clock #(.highDuration(1), .lowDuration(1)) clock_1 (.out(CLK));
  or or_1 (or_1_out, Addr[13], Addr[14]);
  not not_1 (not_1_out, Addr[13]);
  not not_2 (not_2_out, Addr[15]);
  not not_3 (not_3_out, Addr[14]);
  not not_4 (not_4_out, Addr[15]);
  not not_5 (not_5_out, Addr[14]);
  not not_6 (not_6_out, Addr[15]);
  not not_7 (not_7_out, Addr[14]);
  not not_8 (not_8_out, R_W_prime);
  not not_9 (not_9_out, MREQ_prime);
  or or_2 (CS1, or_1_out, Addr[15]);
  or or_3 (or_3_out, not_1_out, Addr[14]);
  or or_4 (CS2, or_3_out, Addr[15]);
  or or_5 (or_5_out, not_2_out, not_3_out);
  or or_6 (or_6_out, or_5_out, not_10_out);
  not not_10 (not_10_out, Addr[13]);
  or or_7 (or_7_out, not_4_out, not_5_out);
  not not_11 (not_11_out, Addr[13]);
  not not_12 (not_12_out, Addr[12]);
  or or_8 (or_8_out, not_6_out, not_7_out);
  not not_13 (not_13_out, Addr[13]);
  not not_14 (not_14_out, Addr[12]);
  not not_15 (not_15_out, Addr[11]);
  and and_1 (ld, R_W_prime, not_9_out);
  and and_2 (str, not_8_out, not_9_out);
  or or_9 (CS3, or_6_out, Addr[12]);
  or or_10 (or_10_out, or_7_out, not_11_out);
  or or_11 (or_11_out, not_12_out, Addr[11]);
  or or_12 (or_12_out, or_8_out, not_13_out);
  or or_13 (or_13_out, not_14_out, not_15_out);
  or or_14 (CS4, or_10_out, or_11_out);
  or or_15 (CS5, or_12_out, or_13_out);
  RAM #(.addrWidth(13), .dataWidth(8), .bus("separate"), .Select("low")) _8k_8bit (
    .addr(Addr[12:0]), .din(Data), .data(Data_2), .str(str), .sel(CS1), .clk(CLK), .ld(ld));  // open: clr
  RAM #(.addrWidth(13), .dataWidth(8), .bus("separate"), .Select("low")) _8k_8bit_2 (
    .addr(Addr[12:0]), .din(Data), .data(Data_2), .str(str), .sel(CS2), .clk(CLK), .ld(ld));  // open: clr
  RAM #(.addrWidth(12), .dataWidth(4), .bus("separate"), .Select("low")) _4k_4bit (
    .addr(Addr[11:0]), .din(Data[7:4]), .data(Data_2[3:0]), .str(str), .sel(CS3), .clk(CLK), .ld(ld));  // open: clr
  ROM #(.addrWidth(11), .dataWidth(8), .Select("low")) _2k_8bit (.addr(Addr[10:0]), .data(Data_2), .sel(CS4));
  ROM #(.addrWidth(11), .dataWidth(8), .Select("low")) _2k_8bit_2 (.addr(Addr[10:0]), .data(Data_2), .sel(CS5));
  RAM #(.addrWidth(12), .dataWidth(4), .bus("separate"), .Select("low")) _4k_4bit_2 (
    .addr(Addr[11:0]), .din(Data[3:0]), .data(Data_2[7:4]), .str(str), .sel(CS3), .clk(CLK), .ld(ld));  // open: clr

  // Other names for the same wires on the sheet: CPU_ADDRESS[15:0] = Addr; A11 = Addr[11]; A12 = Addr[12];
  //   A13 = Addr[13]; A14 = Addr[14]; A15 = Addr[15]; CPU_DATA_IN[7:0] = Data_2; CPU_DATA_OUT[7:0] = Data
endmodule

// ALU
module \算术逻辑运算单元ALU  (
  input  [31:0] X,
  input  [31:0] Y,
  input  [2:0] AluOP,
  output \是否相等 ,
  output [31:0] Result
);

  wire comparator_1_lt;
  wire [24:0] \运算指示 ;
  wire [31:0] adder_1_out, AND_out, bit_extender_1_out, multiplexer_1_out, multiplexer_2_out, not_1_out,
       OR_out, subtractor_1_out;

  // Probe on X
  // Probe on X
  // Probe on Y
  // Probe on Y
  assign not_1_out = ~Y;  // NOT_Gate not_1, 32 bits wide
  // Probe on AluOP
  Multiplexer #(.select(1), .width(32), .disabled("Z"), .enable("false")) multiplexer_1 (
    .in0(Y), .in1(not_1_out), .out(multiplexer_1_out), .sel(AluOP[2]));
  // Probe on Result
  // Probe on Result
  Adder #(.width(32)) adder_1 (.a(X), .b(Y), .out(adder_1_out));  // open: cin, cout
  Subtractor #(.width(32)) subtractor_1 (.a(X), .b(Y), .out(subtractor_1_out));  // open: bin, bout
  assign AND_out = X & multiplexer_1_out;  // AND_Gate AND, 32 bits wide
  assign OR_out = X | multiplexer_1_out;  // OR_Gate OR, 32 bits wide
  Comparator #(.width(32), .mode("twosComplement")) comparator_1 (.a(X), .b(Y), .lt(comparator_1_lt));  // open: gt, eq
  DotMatrix #(.inputtype("column"), .matrixcols(5), .matrixrows(5), .persist(0), .dotshape("square")) dotmatrix_1 (
    .col0(\运算指示 [24:20]), .col1(\运算指示 [19:15]), .col2(\运算指示 [14:10]), .col3(\运算指示 [9:5]), .col4(\运算指示 [4:0]));
  Multiplexer #(.select(1), .width(32), .disabled("Z"), .enable("false")) multiplexer_2 (
    .in0(adder_1_out), .in1(subtractor_1_out), .out(multiplexer_2_out), .sel(AluOP[2]));
  assign bit_extender_1_out = {{31{1'b0}}, comparator_1_lt};  // Bit_Extender bit_extender_1
  Multiplexer #(.select(2), .width(32), .disabled("Z"), .enable("false")) multiplexer_3 (
    .in0(AND_out), .in1(OR_out), .in2(multiplexer_2_out), .in3(bit_extender_1_out), .out(Result),
    .sel(AluOP[1:0]));
  Multiplexer #(.select(3), .width(25), .disabled("Z"), .enable("false")) multiplexer_4 (
    .in0(25'h124081), .in1(25'h1020490), .in2(25'h427c84), .in3({25{1'b0}}), .in4(25'h124091),
    .in5(25'h1020490), .in6(25'h421084), .in7(25'h402811), .out(\运算指示 ), .sel(AluOP));
  Comparator #(.width(32), .mode("twosComplement")) comparator_2 (
    .a(Result), .b({32{1'b0}}), .eq(\是否相等 ));  // open: gt, lt

  // Other names for the same wires on the sheet: S[2:0] = AluOP; Zero = \是否相等 

  // Notes on the sheet:
  //   Y: pull=down
  //   X: pull=down
  //   AluOP: pull=down
  //   不要改变此引脚区域内容，也不要改变ALU封装形式
  //   请在下方利用上方输入输出引脚的隧道信号构建ALU电路，ctrl+d复制选择部件
  //   输入引脚
  //   探测区域
  //   输出引脚
  //   功能说明：  AluOP                   AluOP
  //   000：X AND Y      100：X AND Y'
  //   001：X OR Y        101：X OR Y'  
  //   010：X + Y           110：X - Y  
  //   011：未使用         111：SLT  
endmodule

module \MIPS_寄存器文件  (
  input  [4:0] A_address,
  input  [31:0] W_data,
  input  [4:0] B_address,
  input  [4:0] W_address,
  input  W_Enable,
  input  CLK,
  output [31:0] A_data,
  output [31:0] B_data
);

  // RegisterFile registerfile_1: pin names not known; wires that end beside it: W_data, CLK, W_Enable, W_address, A_address, B_address, A_data, B_data

  // Other names for the same wires on the sheet: A_addr[4:0] = A_address; B_addr[4:0] = B_address;
  //   W_addr[4:0] = W_address

  // Notes on the sheet:
  //   输入引脚
  //   输出引脚
endmodule

module \单周期处理器数据路径  (
);

  wire ALUSrc, Branch, clock_1_out, clock_2_out, clock_3_out, function1_1_aluop1, function1_1_alupop0, JUMP,
       MemToReg, MemWrite, PCsrc, RegDst, RegWrite, sll, zero;
  wire [2:0] ALUConrol;
  wire [4:0] multiplexer_3_out;
  wire [5:0] \function , Op;
  wire [25:0] shifter_1_out;
  wire [25:6] rom_1_out_2;
  wire [31:0] adder_1_out, adder_2_out, bit_extender_1_out, \mips_寄存器文件_1_a_data , \mips_寄存器文件_1_b_data ,
       multiplexer_1_out, multiplexer_2_out, multiplexer_4_out, multiplexer_5_out, multiplexer_6_out,
       register_1_q, shifter_2_out, shifter_3_out, \数据存储器_1_rd , \算术逻辑运算单元alu_1_result ;

  Multiplexer #(.select(1), .width(32), .disabled("Z"), .enable("false")) multiplexer_1 (
    .in0(adder_1_out), .in1(adder_2_out), .out(multiplexer_1_out), .sel(PCsrc));
  Multiplexer #(.select(1), .width(32), .disabled("Z"), .enable("false")) multiplexer_2 (
    .in0(multiplexer_1_out), .in1({adder_1_out[31:26], shifter_1_out}), .out(multiplexer_2_out), .sel(JUMP));
  Register #(.width(32), .trigger("rising"), .Select("low")) register_1 (
    .D(multiplexer_2_out), .Q(register_1_q), .clk(clock_1_out));  // open: en, clr
  Clock #(.highDuration(1), .lowDuration(1)) clock_1 (.out(clock_1_out));
  function1 function1_1 (
    .OP0(Op[0]), .OP1(Op[1]), .OP2(Op[2]), .OP3(Op[3]), .OP4(Op[4]), .OP5(Op[5]),
    .ALUPOP0(function1_1_alupop0), .ALUOP1(function1_1_aluop1), .RegWrite(RegWrite), .RegDst(RegDst),
    .AluSrc(ALUSrc), .Branch(Branch), .MemWrite(MemWrite), .MemtoReg(MemToReg), .JUMP(JUMP));
  ROM rom_1 (.in_1(register_1_q), .out_2({Op, rom_1_out_2, \function }));
  Adder #(.width(32)) adder_1 (.a(register_1_q), .b(32'h4), .out(adder_1_out));  // open: cin, cout
  function2 function2_1 (
    .ALUOP0(function1_1_alupop0), .ALUOP1(function1_1_aluop1), .F0(\function [0]), .F1(\function [1]),
    .F2(\function [2]), .F3(\function [3]), .F4(\function [4]), .F5(\function [5]), .A0(ALUConrol[0]),
    .A1(ALUConrol[1]), .A2(ALUConrol[2]), .sll(sll));
  Clock #(.highDuration(1), .lowDuration(1)) clock_2 (.out(clock_2_out));
  \MIPS_寄存器文件  \mips_寄存器文件_1  (
    .A_address(rom_1_out_2[25:21]), .W_data(multiplexer_6_out), .A_data(\mips_寄存器文件_1_a_data ),
    .B_data(\mips_寄存器文件_1_b_data ), .B_address(rom_1_out_2[20:16]), .W_address(multiplexer_3_out),
    .W_Enable(RegWrite), .CLK(clock_2_out));
  Shifter #(.width(26), .shift("ll")) shifter_1 (
    .in({rom_1_out_2, \function }), .\dist (5'b00010), .out(shifter_1_out));
  assign bit_extender_1_out = {{16{rom_1_out_2[15]}}, {rom_1_out_2[15:6], \function }};  // Bit_Extender bit_extender_1
  Multiplexer #(.select(1), .width(5), .disabled("Z"), .enable("false")) multiplexer_3 (
    .in0(rom_1_out_2[15:11]), .in1(rom_1_out_2[10:6]), .out(multiplexer_3_out), .sel(RegDst));
  Shifter #(.width(32), .shift("ll")) shifter_2 (
    .in(\mips_寄存器文件_1_b_data ), .\dist (rom_1_out_2[10:6]), .out(shifter_2_out));
  Shifter #(.width(32), .shift("ll")) shifter_3 (.in(bit_extender_1_out), .\dist (5'b00010), .out(shifter_3_out));
  Multiplexer #(.select(1), .width(32), .disabled("Z"), .enable("false")) multiplexer_4 (
    .in0(\mips_寄存器文件_1_b_data ), .in1(bit_extender_1_out), .out(multiplexer_4_out), .sel(ALUSrc));
  Adder #(.width(32)) adder_2 (.a(shifter_3_out), .b(adder_1_out), .out(adder_2_out));  // open: cin, cout
  and and_1 (PCsrc, Branch, zero);
  Multiplexer #(.select(1), .width(32), .disabled("Z"), .enable("false")) multiplexer_5 (
    .in0(multiplexer_4_out), .in1(shifter_2_out), .out(multiplexer_5_out), .sel(sll));
  \算术逻辑运算单元ALU  \u_算术逻辑运算单元alu_1  (
    .AluOP(ALUConrol), .X(\mips_寄存器文件_1_a_data ), .Result(\算术逻辑运算单元alu_1_result ), .Y(multiplexer_5_out),
    .\是否相等 (zero));
  Clock #(.highDuration(1), .lowDuration(1)) clock_3 (.out(clock_3_out));
  \数据存储器  \u_数据存储器_1  (
    .A(\算术逻辑运算单元alu_1_result ), .WD(\mips_寄存器文件_1_b_data ), .WE(MemWrite), .CLK(clock_3_out),
    .RD(\数据存储器_1_rd ));
  Multiplexer #(.select(1), .width(32), .disabled("Z"), .enable("false")) multiplexer_6 (
    .in0(\算术逻辑运算单元alu_1_result ), .in1(\数据存储器_1_rd ), .out(multiplexer_6_out), .sel(MemToReg));

  // Notes on the sheet:
  //   PCJUMP
  //   sll
endmodule

// FA
module \一位全加器FA封装1  (
  input  Cin,
  input  Xi,
  input  Yi,
  output Cout,
  output Si
);

  wire AND_2_out, AND_out, XOR_2_out;

  or OR (Cout, AND_out, AND_2_out);
  and AND (AND_out, Xi, Yi);
  and AND_2 (AND_2_out, Cin, XOR_2_out);
  xor XOR (Si, Cin, XOR_2_out);
  xor XOR_2 (XOR_2_out, Xi, Yi);

  // Notes on the sheet:
  //   Yi: pull=down
  //   Xi: pull=down
  //   Cin: pull=down
  //   Si = Xi ^ Yi ^ Cin
  //   Cout = Xi Yi + Cin (Xi ^ Yi)
endmodule

module \_8位串行加法器  (
  input  [7:0] X,
  input  [7:0] Y,
  input  Cin,
  output [7:0] S,
  output Cout,
  output Overflow
);

  wire \一位全加器fa封装1_2_cout , \一位全加器fa封装1_3_cout , \一位全加器fa封装1_4_cout , \一位全加器fa封装1_5_cout ,
       \一位全加器fa封装1_6_cout , \一位全加器fa封装1_7_cout , \一位全加器fa封装1_8_cout ;

  xor xor_1 (Overflow, Cout, \一位全加器fa封装1_2_cout );
  \一位全加器FA封装1  \u_一位全加器fa封装1_1  (.Cout(Cout), .Si(S[7]), .Cin(\一位全加器fa封装1_2_cout ), .Xi(X[7]), .Yi(Y[7]));
  \一位全加器FA封装1  \u_一位全加器fa封装1_2  (
    .Cout(\一位全加器fa封装1_2_cout ), .Si(S[6]), .Cin(\一位全加器fa封装1_3_cout ), .Xi(X[6]), .Yi(Y[6]));
  \一位全加器FA封装1  \u_一位全加器fa封装1_3  (
    .Cout(\一位全加器fa封装1_3_cout ), .Si(S[5]), .Cin(\一位全加器fa封装1_4_cout ), .Xi(X[5]), .Yi(Y[5]));
  \一位全加器FA封装1  \u_一位全加器fa封装1_4  (
    .Cout(\一位全加器fa封装1_4_cout ), .Si(S[4]), .Cin(\一位全加器fa封装1_5_cout ), .Xi(X[4]), .Yi(Y[4]));
  \一位全加器FA封装1  \u_一位全加器fa封装1_5  (
    .Cout(\一位全加器fa封装1_5_cout ), .Si(S[3]), .Cin(\一位全加器fa封装1_6_cout ), .Xi(X[3]), .Yi(Y[3]));
  \一位全加器FA封装1  \u_一位全加器fa封装1_6  (
    .Cout(\一位全加器fa封装1_6_cout ), .Si(S[2]), .Cin(\一位全加器fa封装1_7_cout ), .Xi(X[2]), .Yi(Y[2]));
  // Probe on X
  // Probe on Y
  // Probe on S
  \一位全加器FA封装1  \u_一位全加器fa封装1_7  (
    .Cout(\一位全加器fa封装1_7_cout ), .Si(S[1]), .Cin(\一位全加器fa封装1_8_cout ), .Xi(X[1]), .Yi(Y[1]));
  // Probe on X
  // Probe on Y
  // Probe on S
  \一位全加器FA封装1  \u_一位全加器fa封装1_8  (.Cout(\一位全加器fa封装1_8_cout ), .Si(S[0]), .Cin(Cin), .Xi(X[0]), .Yi(Y[0]));

  // Other names for the same wires on the sheet: OF = Overflow

  // Notes on the sheet:
  //   X: pull=down
  //   Cin: pull=down
  //   Y: pull=down
  //   输入引脚区
  //   符号位
  //   输出引脚区
  //   +
  //   =
  //   有符号加法
  //   +
  //   =
  //   无符号加法
endmodule

module trace (
  input  [7:0] in_1,
  output [31:0] X,
  output [31:0] Y,
  output [2:0] AluOP,
  output [31:0] R,
  output Zero
);

  ROM #(.addrWidth(8), .dataWidth(32), .Select("high")) rom_1 (.addr(in_1), .data(X));
  ROM #(.addrWidth(8), .dataWidth(32), .Select("high")) rom_2 (.addr(in_1), .data(Y));
  ROM #(.addrWidth(8), .dataWidth(3), .Select("high")) rom_3 (.addr(in_1), .data(AluOP));
  ROM #(.addrWidth(8), .dataWidth(32), .Select("high")) rom_4 (.addr(in_1), .data(R));
  ROM #(.addrWidth(8), .dataWidth(1), .Select("high")) rom_5 (.addr(in_1), .data(Zero));

  // Notes on the sheet:
  //   X trace
  //   contents of rom_1 (hex, n*v repeats v):
  //   1 1 1 0 11111111 0 0 0 10b67f2
  //   Y trace
  //   contents of rom_2 (hex, n*v repeats v):
  //   1 0 1 4*0 1 2f5a0df4
  //   ALU OP Trace
  //   contents of rom_3 (hex, n*v repeats v):
  //   0 1 2 0 4 5 6 7 2
  //   Result
  //   contents of rom_4 (hex, n*v repeats v):
  //   1 1 2 0 11111111 ffffffff 0 1 306575e6
  //   Zero Flag
  //   contents of rom_5 (hex, n*v repeats v):
  //   0 0 0 1 0 0 1 0 0 247*1
endmodule

module \ALU自动测试  (
  output [7:0] TEST_num
);

  wire ADD, AND, and_1_out, AND_prime, CLK, HALT, Halt_t, multiplexer_1_out, nHalt, NotEQ, OR, OR_prime,
       priority_encoder_1_gs, Rok, SLT, SUB, X___Y, X___Y_t, X_AND_Y, X_AND_Y_prime, X_OR_Y, X_OR_Y_prime,
       X_Y, xnor_1_out, Zero, Zero_Standard, \悬空检测 ;
  wire [2:0] ALUOP;
  wire [3:0] \个位 , \十位 , \百位 ;
  wire [7:0] adder_1_out, \单项评分_1_总条数 , \单项评分_1_扣分 , \单项评分_1_正确条数 , \单项评分_2_总条数 , \单项评分_2_扣分 , \单项评分_2_正确条数 ,
       \单项评分_3_总条数 , \单项评分_3_扣分 , \单项评分_3_正确条数 , \单项评分_4_总条数 , \单项评分_4_扣分 , \单项评分_4_正确条数 , \单项评分_5_总条数 ,
       \单项评分_5_扣分 , \单项评分_5_正确条数 , \单项评分_6_总条数 , \单项评分_6_扣分 , \单项评分_6_正确条数 , \单项评分_7_总条数 , \单项评分_7_扣分 ,
       \单项评分_7_正确条数 , \单项评分_8_扣分 , \总项评分_1_总分 ;
  wire [9:0] counter_1_q;
  wire [31:0] bit_extender_1_out, R, R_Standard, X, Y;

  Register #(.width(8), .trigger("rising"), .Select("low")) register_1 (
    .D(adder_1_out), .en(nHalt), .Q(TEST_num), .clk(CLK));  // open: clr
  Clock #(.highDuration(1), .lowDuration(1)) clock_1 (.out(CLK));
  \单项评分  \u_单项评分_1  (
    .ALUOP(AND), .\扣分 (\单项评分_1_扣分 ), .\正确条数 (\单项评分_1_正确条数 ), .Rok(Rok), .nHalt(nHalt), .Right(X_AND_Y),
    .CLK(CLK), .\总条数 (\单项评分_1_总条数 ), .NotEQ(NotEQ));
  // Probe on \单项评分_1_总条数 
  // Probe on \单项评分_1_正确条数 
  // Probe on \单项评分_1_扣分 
  Adder #(.width(8)) adder_1 (.a(8'h1), .b(TEST_num), .out(adder_1_out));  // open: cin, cout
  not not_1 (nHalt, Halt_t);
  Comparator #(.width(3), .mode("twosComplement")) comparator_1 (.a(ALUOP), .b(3'b011), .eq(Halt_t));  // open: gt, lt
  Counter #(.width(10), .max('h3ff), .ongoal("wrap"), .trigger("rising"), .behavior("old")) counter_1 (
    .count(NotEQ), .Q(counter_1_q), .clk(CLK), .clr(Halt_t));  // open: load, D, carry, preset
  and and_1 (and_1_out, ~Halt_t, NotEQ);  // AND_Gate
  \单项评分  \u_单项评分_2  (
    .ALUOP(OR), .\扣分 (\单项评分_2_扣分 ), .\正确条数 (\单项评分_2_正确条数 ), .Rok(Rok), .nHalt(nHalt), .Right(X_OR_Y),
    .CLK(CLK), .\总条数 (\单项评分_2_总条数 ), .NotEQ(NotEQ));
  // Probe on \单项评分_2_总条数 
  // Probe on \单项评分_2_正确条数 
  // Probe on \单项评分_2_扣分 
  \总项评分  \u_总项评分_1  (
    .in_1(\单项评分_1_扣分 ), .in_2(\单项评分_2_扣分 ), .in_3(\单项评分_3_扣分 ), .in_4(\单项评分_4_扣分 ), .in_5(\单项评分_5_扣分 ),
    .in_6(\单项评分_6_扣分 ), .in_8(\单项评分_7_扣分 ), .in_9(\单项评分_8_扣分 ), .\总分 (\总项评分_1_总分 ), .\百位 (\百位 ), .\十位 (\十位 ),
    .\个位 (\个位 ), .\Zero悬空扣分 (\悬空检测 ));
  trace trace_1 (.in_1(TEST_num), .X(X), .Y(Y), .AluOP(ALUOP), .R(R_Standard), .Zero(Zero_Standard));
  \单项评分  \u_单项评分_3  (
    .ALUOP(ADD), .\扣分 (\单项评分_3_扣分 ), .\正确条数 (\单项评分_3_正确条数 ), .Rok(Rok), .nHalt(nHalt), .Right(X___Y),
    .CLK(CLK), .\总条数 (\单项评分_3_总条数 ), .NotEQ(NotEQ));
  // Probe on \单项评分_3_总条数 
  // Probe on \单项评分_3_正确条数 
  // Probe on \单项评分_3_扣分 
  RAM #(.addrWidth(10), .dataWidth(32), .bus("separate"), .Select("low")) ram_1 (
    .addr(counter_1_q), .din(X), .str(and_1_out), .clk(CLK));  // open: data, sel, ld, clr
  \单项评分  \u_单项评分_4  (
    .ALUOP(AND_prime), .\扣分 (\单项评分_4_扣分 ), .\正确条数 (\单项评分_4_正确条数 ), .Rok(Rok), .nHalt(nHalt),
    .Right(X_AND_Y_prime), .CLK(CLK), .\总条数 (\单项评分_4_总条数 ), .NotEQ(NotEQ));
  // Probe on \单项评分_4_总条数 
  // Probe on \单项评分_4_正确条数 
  // Probe on \单项评分_4_扣分 
  \单项评分  \u_单项评分_5  (
    .ALUOP(OR_prime), .\扣分 (\单项评分_5_扣分 ), .\正确条数 (\单项评分_5_正确条数 ), .Rok(Rok), .nHalt(nHalt),
    .Right(X_OR_Y_prime), .CLK(CLK), .\总条数 (\单项评分_5_总条数 ), .NotEQ(NotEQ));
  // Probe on \单项评分_5_总条数 
  // Probe on \单项评分_5_正确条数 
  // Probe on \单项评分_5_扣分 
  // Probe on \总项评分_1_总分 
  \算术逻辑运算单元ALU  \u_算术逻辑运算单元alu_1  (.AluOP(ALUOP), .X(X), .Result(R), .Y(Y), .\是否相等 (Zero));
  RAM #(.addrWidth(10), .dataWidth(32), .bus("separate"), .Select("low")) ram_2 (
    .addr(counter_1_q), .din(Y), .str(and_1_out), .clk(CLK));  // open: data, sel, ld, clr
  assign bit_extender_1_out = {{29{1'b0}}, ALUOP};  // Bit_Extender bit_extender_1
  \单项评分  \u_单项评分_6  (
    .ALUOP(SUB), .\扣分 (\单项评分_6_扣分 ), .\正确条数 (\单项评分_6_正确条数 ), .Rok(Rok), .nHalt(nHalt), .Right(X___Y_t),
    .CLK(CLK), .\总条数 (\单项评分_6_总条数 ), .NotEQ(NotEQ));
  // Probe on \单项评分_7_总条数 
  // Probe on \单项评分_6_总条数 
  // Probe on \单项评分_6_正确条数 
  // Probe on \单项评分_6_扣分 
  \单项评分  \u_单项评分_7  (
    .ALUOP(SLT), .\扣分 (\单项评分_7_扣分 ), .\正确条数 (\单项评分_7_正确条数 ), .Rok(Rok), .nHalt(nHalt), .Right(X_Y),
    .CLK(CLK), .\总条数 (\单项评分_7_总条数 ), .NotEQ(NotEQ));
  // Probe on \单项评分_7_正确条数 
  // Probe on \单项评分_7_扣分 
  // Probe on ALUOP
  \单项评分  \u_单项评分_8  (
    .ALUOP(1'b0), .\扣分 (\单项评分_8_扣分 ), .Rok(Rok), .nHalt(nHalt), .CLK(CLK), .NotEQ(NotEQ));  // open: 正确条数, Right, 总条数
  RAM #(.addrWidth(10), .dataWidth(32), .bus("separate"), .Select("low")) ram_3 (
    .addr(counter_1_q), .din(bit_extender_1_out), .str(and_1_out), .clk(CLK));  // open: data, sel, ld, clr
  Decoder #(.select(3), .tristate("false"), .disabled("Z"), .enable("false")) decoder_1 (
    .out0(AND), .out1(OR), .out2(ADD), .out3(HALT), .out4(AND_prime), .out5(OR_prime), .out6(SUB),
    .out7(SLT), .sel(ALUOP));
  Multiplexer #(.select(1), .width(1), .disabled("Z"), .enable("false")) multiplexer_1 (
    .in0(1'b1), .in1(1'b1), .out(multiplexer_1_out), .sel(Zero));
  xnor xnor_1 (xnor_1_out, Zero_Standard, Zero);
  Comparator #(.width(32), .mode("twosComplement")) comparator_2 (.a(R_Standard), .b(R), .eq(Rok));  // open: gt, lt
  LED #(.active("false")) led_1 (.in(X_AND_Y));
  LED #(.active("false")) led_2 (.in(X_OR_Y));
  LED #(.active("false")) led_3 (.in(X___Y));
  LED #(.active("false")) led_4 (.in(X_AND_Y_prime));
  LED #(.active("false")) led_5 (.in(X_OR_Y_prime));
  LED #(.active("false")) led_6 (.in(X___Y_t));
  LED #(.active("false")) led_7 (.in(X_Y));
  LED #(.active("true")) led_8 (.in(NotEQ));
  Priority_Encoder #(.select(1), .disabled("Z")) priority_encoder_1 (
    .in0(multiplexer_1_out), .in1(multiplexer_1_out), .gs(priority_encoder_1_gs));  // open: out, en_out, en_in
  not not_2 (\悬空检测 , priority_encoder_1_gs);
  nand nand_1 (NotEQ, xnor_1_out, Rok);
  Hex_Digit_Display hex_digit_display_1 (.value(\百位 ));  // open: dp
  Hex_Digit_Display hex_digit_display_2 (.value(\个位 ));  // open: dp
  Hex_Digit_Display hex_digit_display_3 (.value(\十位 ));  // open: dp

  // Notes on the sheet:
  //   X 错误记录
  //   Y 错误记录
  //   ALUOP 错误记录
  //   运算故障指示
  //   红色异常
  //   成绩
endmodule

module \单项评分  (
  input  ALUOP,
  input  NotEQ,
  input  Rok,
  input  nHalt,
  input  CLK,
  output [7:0] \扣分 ,
  output [7:0] \正确条数 ,
  output Right,
  output [7:0] \总条数 
);

  wire and_1_out, and_2_out, and_3_out, and_4_out, comparator_1_eq, not_1_out, not_2_out, not_3_out,
       undriven, undriven_2, undriven_3, undriven_4;
  wire [7:0] counter_1_q, counter_2_q, multiplexer_1_out;

  not not_1 (not_1_out, NotEQ);
  and and_1 (and_1_out, undriven, undriven_2, undriven_3);
  and and_2 (and_2_out, undriven, undriven_3);
  and and_3 (and_3_out, ALUOP, not_1_out, Rok, nHalt);
  and and_4 (and_4_out, ALUOP, nHalt);
  Counter #(.width(8), .max('hff), .ongoal("wrap"), .trigger("rising"), .behavior("new")) counter_1 (
    .Q(counter_1_q), .clk(undriven_4), .down(and_1_out));  // open: load, D, count, carry, clr, preset
  Counter #(.width(8), .max('hff), .ongoal("wrap"), .trigger("rising"), .behavior("new")) counter_2 (
    .Q(counter_2_q), .down(and_2_out));  // open: load, D, count, carry, clk, clr, preset
  Counter #(.width(8), .max('hff), .ongoal("wrap"), .trigger("rising"), .behavior("old")) counter_3 (
    .count(and_3_out), .Q(\正确条数 ), .clk(CLK));  // open: load, D, carry, clr, preset
  Counter #(.width(8), .max('hff), .ongoal("wrap"), .trigger("rising"), .behavior("old")) counter_4 (
    .count(and_4_out), .Q(\总条数 ), .clk(CLK));  // open: load, D, carry, clr, preset
  Comparator #(.width(8), .mode("twosComplement")) comparator_1 (
    .a(counter_1_q), .b(counter_2_q), .eq(comparator_1_eq));  // open: gt, lt
  Comparator #(.width(8), .mode("twosComplement")) comparator_2 (.a(\正确条数 ), .b(\总条数 ), .eq(Right));  // open: gt, lt
  Multiplexer #(.select(1), .width(8), .disabled("Z"), .enable("false")) multiplexer_1 (
    .in0({8{1'b0}}), .in1(8'h5), .out(multiplexer_1_out), .sel(not_2_out));
  not not_2 (not_2_out, comparator_1_eq);
  not not_3 (not_3_out, Right);
  Multiplexer #(.select(1), .width(8), .disabled("Z"), .enable("false")) multiplexer_2 (
    .in0({8{1'b0}}), .in1(8'h5), .out(\扣分 ), .sel(not_3_out));

  // Notes on the sheet:
  //   ALUOP
  //   Rok
  //   ~Halt
  //   CLK
  //   Duplicated
  //   总条数
  //   正确条数
  //   扣分
  //   Right？
endmodule

module \总项评分  (
  input  [7:0] in_1,
  input  [7:0] in_2,
  input  [7:0] in_3,
  input  [7:0] in_4,
  input  [7:0] in_5,
  input  [7:0] in_6,
  input  \Zero悬空扣分 ,
  input  [7:0] in_8,
  input  [7:0] in_9,
  output [7:0] \总分 ,
  output [3:0] \百位 ,
  output [3:0] \十位 ,
  output [3:0] \个位 
);

  wire [7:0] adder_1_out, adder_2_out, adder_3_out, adder_4_out, adder_5_out, adder_6_out, adder_7_out,
       divider_1_out, subtractor_1_out, subtractor_2_out;
  wire [7:4] divider_1_rem, divider_2_out, divider_2_rem;

  Adder #(.width(8)) adder_1 (.a(in_1), .b(in_2), .out(adder_1_out));  // open: cin, cout
  Adder #(.width(8)) adder_2 (.a(in_3), .b(in_4), .out(adder_2_out));  // open: cin, cout
  Adder #(.width(8)) adder_3 (.a(in_5), .b(in_6), .out(adder_3_out));  // open: cin, cout
  Adder #(.width(8)) adder_4 (.a(in_8), .b(in_9), .out(adder_4_out));  // open: cin, cout
  Adder #(.width(8)) adder_5 (.a(adder_1_out), .b(adder_2_out), .out(adder_5_out));  // open: cin, cout
  Adder #(.width(8)) adder_6 (.a(adder_3_out), .b(adder_4_out), .out(adder_6_out));  // open: cin, cout
  Adder #(.width(8)) adder_7 (.a(adder_5_out), .b(adder_6_out), .out(adder_7_out));  // open: cin, cout
  Subtractor #(.width(8)) subtractor_1 (.a(8'h64), .b(adder_7_out), .out(subtractor_1_out));  // open: bin, bout
  Subtractor #(.width(8)) subtractor_2 (.a(subtractor_1_out), .b(8'h5), .out(subtractor_2_out));  // open: bin, bout
  Multiplexer #(.select(1), .width(8), .disabled("Z"), .enable("false")) multiplexer_1 (
    .in0(subtractor_1_out), .in1(subtractor_2_out), .out(\总分 ), .sel(\Zero悬空扣分 ));
  Divider #(.width(8)) divider_1 (.a(\总分 ), .b(8'ha), .out(divider_1_out), .rem({divider_1_rem, \个位 }));  // open: upper
  Divider #(.width(8)) divider_2 (
    .a(divider_1_out), .b(8'ha), .out({divider_2_out, \百位 }), .rem({divider_2_rem, \十位 }));  // open: upper
endmodule

module decode1 (
  input  A15,
  input  A14,
  input  A13,
  output CS1,
  output CS2
);

  wire not_1_out, or_1_out, or_3_out;

  or or_1 (or_1_out, A13, A14);
  not not_1 (not_1_out, A13);
  or or_2 (CS1, or_1_out, A15);
  or or_3 (or_3_out, not_1_out, A14);
  or or_4 (CS2, or_3_out, A15);
endmodule

module decode2 (
  input  A15,
  input  A14,
  input  A13,
  output CS3
);

  wire not_1_out, not_2_out, not_3_out, or_1_out;

  not not_1 (not_1_out, A15);
  not not_2 (not_2_out, A14);
  or or_1 (or_1_out, not_1_out, not_2_out);
  not not_3 (not_3_out, A13);
  or or_2 (CS3, or_1_out, not_3_out);
endmodule

module decode3 (
  input  A15,
  input  A14,
  input  A13,
  input  A12,
  input  A11,
  output CS4,
  output CS5
);

  wire not_1_out, not_2_out, not_3_out, not_4_out, not_5_out, not_6_out, not_7_out, not_8_out, not_9_out,
       or_1_out, or_2_out, or_3_out, or_5_out, or_6_out, or_8_out;

  not not_1 (not_1_out, A15);
  not not_2 (not_2_out, A14);
  not not_3 (not_3_out, A15);
  not not_4 (not_4_out, A14);
  or or_1 (or_1_out, not_1_out, not_2_out);
  not not_5 (not_5_out, A13);
  not not_6 (not_6_out, A12);
  or or_2 (or_2_out, not_3_out, not_4_out);
  not not_7 (not_7_out, A13);
  not not_8 (not_8_out, A12);
  not not_9 (not_9_out, A11);
  or or_3 (or_3_out, or_1_out, not_5_out);
  or or_4 (CS4, or_3_out, or_5_out);
  or or_5 (or_5_out, not_6_out, A11);
  or or_6 (or_6_out, or_2_out, not_7_out);
  or or_7 (CS5, or_6_out, or_8_out);
  or or_8 (or_8_out, not_8_out, not_9_out);
endmodule

module funct_R (
  input  F0,
  input  F1,
  input  F2,
  input  F3,
  input  F4,
  input  F5,
  output OP0,
  output OP1,
  output OP2
);

  wire and_1_out;

  not not_1 (OP1, F3);
  and and_1 (and_1_out, F3, F4);
  or or_1 (OP2, F5, and_1_out);

  assign OP0 = F4;
endmodule

module opcode (
  input  O0,
  input  O1,
  input  O2,
  input  O3,
  input  O4,
  input  O5,
  output F0,
  output F1,
  output F2,
  output F3,
  output F4,
  output F5
);


  assign F0 = 1'b1;
  assign F1 = 1'b1;
  assign F2 = 1'b1;
  assign F3 = 1'b1;
  assign F4 = 1'b1;
  assign F5 = 1'b1;
endmodule

module function1 (
  input  OP0,
  input  OP1,
  input  OP2,
  input  OP3,
  input  OP4,
  input  OP5,
  output ALUPOP0,
  output ALUOP1,
  output RegWrite,
  output RegDst,
  output AluSrc,
  output Branch,
  output MemWrite,
  output MemtoReg,
  output JUMP
);

  wire not_1_out, not_2_out, not_3_out, not_4_out, not_6_out, not_7_out, not_8_out, not_9_out, not_10_out;

  not not_1 (not_1_out, OP3);
  not not_2 (not_2_out, OP4);
  not not_3 (not_3_out, OP2);
  not not_4 (not_4_out, OP3);
  not not_5 (RegDst, OP4);
  not not_6 (not_6_out, OP0);
  not not_7 (not_7_out, OP1);
  not not_8 (not_8_out, OP2);
  not not_9 (not_9_out, OP3);
  not not_10 (not_10_out, OP5);
  and and_1 (ALUPOP0, not_1_out, not_2_out);
  and and_2 (RegWrite, not_3_out, not_4_out);
  and and_3 (JUMP, not_6_out, not_7_out, not_8_out, not_9_out, OP4, not_10_out);

  assign ALUOP1 = OP3;
  assign AluSrc = OP4;
  assign Branch = OP3;
  assign MemtoReg = OP4;
  assign MemWrite = OP2;
endmodule

module function2 (
  input  ALUOP0,
  input  ALUOP1,
  input  F0,
  input  F1,
  input  F2,
  input  F3,
  input  F4,
  input  F5,
  output A0,
  output A1,
  output A2,
  output sll
);

  wire and_1_out, and_2_out, and_3_out, and_4_out, not_1_out, not_2_out, not_3_out, not_4_out, not_5_out,
       not_6_out, not_7_out, not_8_out, not_9_out, not_10_out, not_11_out, not_12_out, not_13_out,
       not_14_out, not_15_out, not_16_out, not_17_out, not_18_out, not_19_out;

  not not_1 (not_1_out, F0);
  not not_2 (not_2_out, F1);
  not not_3 (not_3_out, F2);
  not not_4 (not_4_out, F3);
  not not_5 (not_5_out, F4);
  not not_6 (not_6_out, F5);
  not not_7 (not_7_out, F1);
  not not_8 (not_8_out, F3);
  not not_9 (not_9_out, F5);
  not not_10 (not_10_out, ALUOP0);
  or or_1 (A1, not_10_out, not_11_out);
  not not_11 (not_11_out, F3);
  and and_1 (and_1_out, ALUOP0, F5);
  and and_2 (and_2_out, ALUOP0, F2);
  not not_12 (not_12_out, ALUOP0);
  not not_13 (not_13_out, ALUOP1);
  not not_14 (not_14_out, F0);
  not not_15 (not_15_out, F1);
  not not_16 (not_16_out, F2);
  not not_17 (not_17_out, F3);
  not not_18 (not_18_out, F4);
  not not_19 (not_19_out, F5);
  and and_3 (and_3_out, ALUOP0, not_1_out, not_2_out, not_3_out, not_4_out, not_5_out, not_6_out);
  and and_4 (and_4_out, ALUOP0, F0, not_7_out, not_8_out, F4, not_9_out);
  or or_2 (A2, and_1_out, and_2_out);
  and and_5 (sll, not_12_out, not_13_out, not_14_out, not_15_out, not_16_out, not_17_out, not_18_out, not_19_out);
  or or_3 (A0, ALUOP1, and_3_out, and_4_out);
endmodule
