// Logisim project 红绿灯.circ as structural Verilog: 6 circuits, main circuit main
module \状态转换  (
  input  S1,
  input  S0,
  input  TA,
  input  TB,
  output S11,
  output S00
);

  wire and_1_out, and_2_out, and_3_out, and_4_out, not_1_out, not_2_out, not_3_out, not_4_out, not_5_out,
       not_6_out, not_7_out;

  not not_1 (not_1_out, S1);
  and and_1 (and_1_out, not_1_out, S0);
  and and_2 (and_2_out, S1, not_2_out);
  not not_2 (not_2_out, S0);
  not not_3 (not_3_out, S1);
  not not_4 (not_4_out, S0);
  and and_3 (and_3_out, not_3_out, not_4_out, not_5_out);
  not not_5 (not_5_out, TA);
  and and_4 (and_4_out, S1, not_6_out, not_7_out);
  not not_6 (not_6_out, S0);
  not not_7 (not_7_out, TB);
  or or_1 (S11, and_1_out, and_2_out);
  or or_2 (S00, and_3_out, and_4_out);
endmodule

module main (
  input  in_1,
  input  in_2
);

  wire A, a_t, and_1_out, and_2_out, B, b_t, C, c_t, Clk, Clk5, clock_1_out, comparator_1_eq,
       comparator_1_gt, D, d_t, dipswitch_1_p1, dipswitch_1_p2, E, e_t, F, f_t, G, g_t, LAG, LAR, LAY, LBG,
       LBR, LBY, or_1_out, register_1_q, register_2_q, \七段_测试电路_1_out_2 , \七段_测试电路_1_out_3 ,
       \七段_测试电路_1_out_4 , \七段_测试电路_1_out_5 , \状态转换_1_s00 , \状态转换_1_s11 , \状态输出_1_la1 , \状态输出_1_la2 ,
       \状态输出_1_lb1 , \状态输出_1_lb2 ;
  wire [3:0] counter_1_q;

  // DipSwitch #(.NSwitches(2)) dipswitch_1: pin names not known; wires that end beside it: dipswitch_1_p1, dipswitch_1_p2
  \七段_测试电路  \u_七段_测试电路_1  (
    .in_1(Clk), .out_2(\七段_测试电路_1_out_2 ), .out_3(\七段_测试电路_1_out_3 ), .out_4(\七段_测试电路_1_out_4 ),
    .out_5(\七段_测试电路_1_out_5 ));
  \状态转换  \u_状态转换_1  (
    .S1(register_1_q), .S0(register_2_q), .TA(dipswitch_1_p1), .TB(dipswitch_1_p2), .S11(\状态转换_1_s11 ),
    .S00(\状态转换_1_s00 ));
  Register #(.width(1), .trigger("rising"), .Select("low")) register_1 (
    .D(\状态转换_1_s11 ), .Q(register_1_q), .clk(Clk5), .clr(in_1));  // open: en
  Register #(.width(1), .trigger("rising"), .Select("low")) register_2 (
    .D(\状态转换_1_s00 ), .Q(register_2_q), .clk(Clk5), .clr(in_2));  // open: en
  Counter #(.width(4), .max('hf), .ongoal("wrap"), .trigger("rising"), .behavior("new")) counter_1 (
    .Q(counter_1_q), .clk(clock_1_out), .clr(Clk5));  // open: load, D, count, carry, preset, down
  Clock #(.highDuration(1), .lowDuration(1)) clock_1 (.out(clock_1_out));
  \状态输出  \u_状态输出_1  (
    .S111(register_1_q), .S000(register_2_q), .LA1(\状态输出_1_la1 ), .LA2(\状态输出_1_la2 ), .LB1(\状态输出_1_lb1 ),
    .LB2(\状态输出_1_lb2 ));
  and and_1 (and_1_out, \七段_测试电路_1_out_4 , \七段_测试电路_1_out_5 );
  and and_2 (and_2_out, \七段_测试电路_1_out_3 , \七段_测试电路_1_out_5 );
  RGB rgb_1 (.IN1(\状态输出_1_la1 ), .IN2(\状态输出_1_la2 ), .G(LAG), .R(LAR), .Y(LAY));
  RGB rgb_2 (.IN1(\状态输出_1_lb1 ), .IN2(\状态输出_1_lb2 ), .G(LBG), .R(LBR), .Y(LBY));
  \七段_译码  \u_七段_译码_1  (
    .A0(\七段_测试电路_1_out_2 ), .A1(\七段_测试电路_1_out_3 ), .A2(\七段_测试电路_1_out_4 ), .A3(\七段_测试电路_1_out_5 ), .A(A),
    .B(B), .C(C), .D(D), .E(E), .F(F), .G(G));
  Comparator #(.width(1), .mode("twosComplement")) comparator_1 (
    .a(and_1_out), .b(and_2_out), .gt(comparator_1_gt), .eq(comparator_1_eq));  // open: lt
  Subtractor #(.width(4)) subtractor_1 (.a(4'b0100), .b(counter_1_q), .bout(Clk5));  // open: out, bin
  or or_1 (or_1_out, comparator_1_gt, comparator_1_eq);
  Clock #(.highDuration(1), .lowDuration(1)) clock_2 (.out(Clk));
  LED #(.active("true")) led_1 (.in(LBG));
  LED #(.active("true")) led_2 (.in(LBR));
  LED #(.active("true")) led_3 (.in(LBY));
  LED #(.active("true")) led_4 (.in(LAR));
  LED #(.active("true")) led_5 (.in(LAG));
  LED #(.active("true")) led_6 (.in(LAY));
  LED #(.active("true")) led_7 (.in(LAY));
  LED #(.active("true")) led_8 (.in(LAR));
  LED #(.active("true")) led_9 (.in(LAG));
  and and_3 (a_t, A, or_1_out);
  and and_4 (b_t, B, or_1_out);
  and and_5 (c_t, C, or_1_out);
  and and_6 (d_t, D, or_1_out);
  and and_7 (e_t, E, or_1_out);
  and and_8 (f_t, F, or_1_out);
  and and_9 (g_t, G, or_1_out);
  LED #(.active("true")) led_10 (.in(LBG));
  LED #(.active("true")) led_11 (.in(LBR));
  LED #(.active("true")) led_12 (.in(LBY));
  _7_Segment_Display #(.active("true")) u_7_segment_display_1 (
    .g(g_t), .f(f_t), .a(a_t), .b(b_t), .e(e_t), .d(d_t), .c(c_t));  // open: dp

  // Notes on the sheet:
  //   TB
  //   TA
  //   LA
  //   LB
endmodule

module \状态输出  (
  input  S111,
  input  S000,
  output LA1,
  output LA2,
  output LB1,
  output LB2
);

  wire not_1_out;

  not not_1 (not_1_out, S111);
  not not_2 (LB1, S111);
  and and_1 (LB2, S111, S000);
  and and_2 (LA2, not_1_out, S000);

  assign LA1 = S111;
endmodule

module RGB (
  input  IN1,
  input  IN2,
  output G,
  output R,
  output Y
);

  wire not_1_out, not_2_out;

  not not_1 (not_1_out, IN1);
  not not_2 (not_2_out, IN2);
  and and_1 (G, not_1_out, not_2_out);

  assign R = IN1;
  assign Y = IN2;
endmodule

module \七段_测试电路  (
  input  in_1,
  output out_2,
  output out_3,
  output out_4,
  output out_5
);

  wire subtractor_1_bout;
  wire [3:0] counter_1_q, subtractor_1_out;

  Counter #(.width(4), .max('hf), .ongoal("wrap"), .trigger("rising"), .behavior("new")) counter_1 (
    .Q(counter_1_q), .clk(in_1), .clr(subtractor_1_bout));  // open: load, D, count, carry, preset, down
  Subtractor #(.width(4)) subtractor_1 (
    .a(4'b0100), .b(counter_1_q), .out(subtractor_1_out), .bout(subtractor_1_bout));  // open: bin
  Adder #(.width(4)) adder_1 (
    .a(4'b0001), .b(subtractor_1_out), .out({out_5, out_4, out_3, out_2}));  // open: cin, cout
endmodule

module \七段_译码  (
  input  A0,
  input  A1,
  input  A2,
  input  A3,
  output A,
  output B,
  output C,
  output D,
  output E,
  output F,
  output G
);

  wire and_1_out, and_2_out, and_3_out, and_4_out, and_5_out, and_6_out, and_7_out, and_8_out, and_9_out,
       and_10_out, and_11_out, and_12_out, and_13_out, and_14_out, and_15_out, and_16_out, and_17_out,
       and_18_out, and_19_out, and_20_out, and_21_out, and_22_out, and_23_out, and_24_out, not_1_out,
       not_2_out, not_3_out, not_4_out, not_5_out, not_6_out, not_7_out, not_8_out, not_9_out, not_10_out,
       not_11_out, not_12_out, not_13_out, not_14_out, not_15_out, not_16_out, not_17_out, not_18_out,
       not_19_out, not_20_out, not_21_out, not_22_out, not_23_out, not_24_out, not_25_out, not_26_out,
       not_27_out, not_28_out, not_29_out, not_30_out, not_31_out, not_32_out, not_33_out, not_34_out,
       not_35_out, not_36_out, not_37_out, not_38_out, not_39_out, not_40_out, not_41_out, not_42_out,
       not_43_out, not_44_out, not_45_out, not_46_out;

  not not_1 (not_1_out, A1);
  and and_1 (and_1_out, not_1_out, not_2_out, A3);
  not not_2 (not_2_out, A2);
  and and_2 (and_2_out, A1, not_3_out);
  not not_3 (not_3_out, A3);
  and and_3 (and_3_out, A0, A2, not_4_out);
  not not_4 (not_4_out, A3);
  not not_5 (not_5_out, A1);
  not not_6 (not_6_out, A2);
  not not_7 (not_7_out, A0);
  not not_8 (not_8_out, A1);
  not not_9 (not_9_out, A3);
  not not_10 (not_10_out, A2);
  not not_11 (not_11_out, A3);
  not not_12 (not_12_out, A3);
  not not_13 (not_13_out, A1);
  and and_4 (and_4_out, not_13_out, not_14_out, A3);
  not not_14 (not_14_out, A2);
  and and_5 (and_5_out, A2, not_15_out);
  not not_15 (not_15_out, A3);
  and and_6 (and_6_out, A0, A1, not_16_out);
  not not_16 (not_16_out, A3);
  not not_17 (not_17_out, A1);
  not not_18 (not_18_out, A2);
  not not_19 (not_19_out, A0);
  not not_20 (not_20_out, A3);
  not not_21 (not_21_out, A2);
  not not_22 (not_22_out, A3);
  not not_23 (not_23_out, A1);
  not not_24 (not_24_out, A3);
  not not_25 (not_25_out, A0);
  not not_26 (not_26_out, A1);
  not not_27 (not_27_out, A2);
  not not_28 (not_28_out, A0);
  not not_29 (not_29_out, A3);
  not not_30 (not_30_out, A1);
  not not_31 (not_31_out, A2);
  not not_32 (not_32_out, A3);
  not not_33 (not_33_out, A1);
  and and_7 (and_7_out, not_33_out, not_34_out, A3);
  not not_34 (not_34_out, A2);
  not not_35 (not_35_out, A0);
  and and_8 (and_8_out, not_35_out, A2, not_36_out);
  not not_36 (not_36_out, A3);
  not not_37 (not_37_out, A1);
  and and_9 (and_9_out, A0, not_37_out, not_38_out);
  not not_38 (not_38_out, A3);
  not not_39 (not_39_out, A1);
  not not_40 (not_40_out, A2);
  and and_10 (and_10_out, not_39_out, not_40_out, A3);
  not not_41 (not_41_out, A1);
  and and_11 (and_11_out, not_41_out, A2, not_42_out);
  not not_42 (not_42_out, A3);
  not not_43 (not_43_out, A0);
  and and_12 (and_12_out, not_43_out, A1, not_44_out);
  not not_44 (not_44_out, A3);
  not not_45 (not_45_out, A2);
  and and_13 (and_13_out, A1, not_45_out, not_46_out);
  not not_46 (not_46_out, A3);
  or or_1 (A, and_1_out, and_2_out, and_3_out);
  and and_14 (and_14_out, not_5_out, not_6_out, A3);
  and and_15 (and_15_out, not_7_out, not_8_out, A2, not_9_out);
  and and_16 (and_16_out, A1, not_10_out, not_11_out);
  and and_17 (and_17_out, A0, A1, not_12_out);
  or or_2 (C, and_4_out, and_5_out, and_6_out);
  and and_18 (and_18_out, not_17_out, not_18_out, A3);
  and and_19 (and_19_out, not_19_out, A1, not_20_out);
  and and_20 (and_20_out, A1, not_21_out, not_22_out);
  and and_21 (and_21_out, A0, not_23_out, A2, not_24_out);
  and and_22 (and_22_out, not_25_out, not_26_out, not_27_out, A3);
  or or_3 (E, and_22_out, and_23_out, and_24_out);
  and and_23 (and_23_out, not_28_out, A1, not_29_out);
  and and_24 (and_24_out, A0, not_30_out, not_31_out, not_32_out);
  or or_4 (F, and_7_out, and_8_out, and_9_out);
  or or_5 (G, and_10_out, and_11_out, and_12_out, and_13_out);
  or or_6 (B, and_14_out, and_15_out, and_16_out, and_17_out);
  or or_7 (D, and_18_out, and_19_out, and_20_out, and_21_out);
endmodule
