// Logisim project 运算指示.circ as structural Verilog
module \运算指示  (
  input  ALUOP1,
  input  ALUOP2,
  input  ALUOP3,
  output AND,
  output OR,
  output ADD,
  output SLT,
  output MUX
);

  wire and_5_out, and_6_out, not_1_out, not_2_out, not_3_out, not_4_out, not_5_out, not_6_out;

  not not_1 (not_1_out, ALUOP2);
  not not_2 (not_2_out, ALUOP3);
  not not_3 (not_3_out, ALUOP2);
  not not_4 (not_4_out, ALUOP3);
  and and_1 (SLT, ALUOP2, ALUOP3);
  not not_5 (not_5_out, ALUOP2);
  not not_6 (not_6_out, ALUOP3);
  and and_2 (AND, not_1_out, not_2_out);
  and and_3 (OR, not_3_out, ALUOP3);
  and and_4 (ADD, ALUOP2, not_4_out);
  and and_5 (and_5_out, ALUOP1, not_5_out);
  and and_6 (and_6_out, ALUOP1, not_6_out);
  or or_1 (MUX, and_5_out, and_6_out);
endmodule
